// Logisim project MILESTONE-3.circ as structural Verilog
module Clock_work (
  input  in_1
);

  wire buzzer_1_p7, clock_1_out, comparator_1_eq, comparator_2_eq, comparator_3_eq, comparator_4_eq,
       comparator_5_eq, j_k_ff_1_q, j_k_ff_2_q, n7_segment_display_1_p1, n7_segment_display_2_p1,
       n7_segment_display_3_p1;
  wire [7:0] counter_1_q;

  Clock clock_1 (.out(clock_1_out));
  Counter #(.max('hf)) counter_1 (.clr(in_1), .clk(clock_1_out), .Q(counter_1_q));  // open: load, up, count, D, carry
  Clock clock_2 ();  // open: out
  // BCD_to_7_Segment_decoder bcd_to_7_segment_decoder_1: pin names not known
  // BCD_to_7_Segment_decoder bcd_to_7_segment_decoder_2: pin names not known
  // _7_Segment_Display 7_segment_display_1: pin names not known; wires that end beside it: n7_segment_display_1_p1, n7_segment_display_1_p1
  // _7_Segment_Display 7_segment_display_2: pin names not known; wires that end beside it: n7_segment_display_2_p1, n7_segment_display_2_p1
  // Binary_to_BCD_converter #(.binvalue(8)) binary_to_bcd_converter_1: pin names not known; wires that end beside it: counter_1_q
  // BCD_to_7_Segment_decoder bcd_to_7_segment_decoder_3: pin names not known
  // _7_Segment_Display 7_segment_display_3: pin names not known; wires that end beside it: n7_segment_display_3_p1, n7_segment_display_3_p1
  LED led_1 (.in(comparator_1_eq));
  Comparator comparator_1 (.a({8{1'b0}}), .b(counter_1_q), .eq(comparator_1_eq));  // open: gt, lt
  Comparator comparator_2 (.a(8'h3), .b(counter_1_q), .eq(comparator_2_eq));  // open: gt, lt
  Comparator comparator_3 (.a(8'hf), .b(counter_1_q), .eq(comparator_3_eq));  // open: gt, lt
  Comparator comparator_4 (.a(8'h4), .b(counter_1_q), .eq(comparator_4_eq));  // open: gt, lt
  Comparator comparator_5 (.a(8'h7), .b(counter_1_q), .eq(comparator_5_eq));  // open: gt, lt
  J_K_Flip_Flop j_k_ff_1 (
    .J(comparator_2_eq), .K(comparator_3_eq), .clk(clock_1_out), .Q(j_k_ff_1_q));  // open: Qn, preset, reset
  // Buzzer buzzer_1: pin names not known; wires that end beside it: 8'h3, 8'hf, 8'h4, 8'h7, 14'h533, comparator_1_eq, buzzer_1_p7, buzzer_1_p7
  J_K_Flip_Flop j_k_ff_2 (
    .J(comparator_4_eq), .K(comparator_5_eq), .clk(clock_1_out), .Q(j_k_ff_2_q));  // open: Qn, preset, reset
  LED led_2 (.in(j_k_ff_1_q));
  // Digital_Oscilloscope #(.nState(20)) digital_oscilloscope_1: pin names not known; wires that end beside it: clock_1_out, comparator_1_eq, j_k_ff_1_q, j_k_ff_2_q
  LED led_3 (.in(j_k_ff_2_q));
  // Buzzer #(.vol_width(32)) buzzer_2: pin names not known; wires that end beside it: 14'h533, j_k_ff_1_q
  // Buzzer buzzer_3: pin names not known; wires that end beside it: 14'h533, j_k_ff_2_q
endmodule

module AND_GATE_v3 (
  input  A,
  input  B,
  output O
);

  wire transistor_1_out, transistor_2_out;

  Transistor #(.\type ("n")) transistor_1 (.in(transistor_2_out), .out(transistor_1_out), .gate(A));
  Transistor #(.\type ("n")) transistor_2 (.in(1'b0), .out(transistor_2_out), .gate(B));
  Pull_Resistor #(.pull(1)) pull_resistor_1 (.node(transistor_1_out));
  Pull_Resistor #(.pull(1)) pull_resistor_2 (.node(O));
  Transistor #(.\type ("n")) transistor_3 (.in(1'b0), .out(O), .gate(transistor_1_out));
endmodule

module OR_GATE_v3 (
  input  A,
  input  B,
  output O
);

  wire nor_gate_v2_1_out_3;

  NOR_GATE_V2 nor_gate_v2_1 (.in_1(A), .in_2(B), .out_3(nor_gate_v2_1_out_3));
  NOT_GATE_v2 not_gate_v2_1 (.A(nor_gate_v2_1_out_3), .O(O));
endmodule

module NOT_GATE_v2 (
  input  A,
  output O
);

  Pull_Resistor #(.pull(1)) pull_resistor_1 (.node(O));
  Transistor #(.\type ("n")) transistor_1 (.in(1'b0), .out(O), .gate(A));
endmodule

module N_AND_GATE_v2 (
  input  A,
  input  B,
  output out_3
);

  wire transistor_2_out;

  Transistor #(.\type ("n")) transistor_1 (.in(transistor_2_out), .out(out_3), .gate(A));
  Transistor #(.\type ("n")) transistor_2 (.in(1'b0), .out(transistor_2_out), .gate(B));
  Pull_Resistor #(.pull(1)) pull_resistor_1 (.node(out_3));
endmodule

module N_OR_GATE (
  input  A,
  input  B,
  output O
);

  wire pull_resistor_1_node, pull_resistor_2_node, transistor_3_out, transistor_4_out, transistor_5_out,
       transistor_6_out;

  Pull_Resistor #(.pull(1)) pull_resistor_1 (.node(pull_resistor_1_node));
  Transistor #(.\type ("n")) transistor_1 (.in(1'b0), .out(pull_resistor_1_node), .gate(A));
  Pull_Resistor #(.pull(1)) pull_resistor_2 (.node(pull_resistor_2_node));
  Transistor #(.\type ("n")) transistor_2 (.in(1'b0), .out(pull_resistor_2_node), .gate(B));
  Transistor #(.\type ("n")) transistor_3 (.in(transistor_4_out), .out(transistor_3_out), .gate(pull_resistor_1_node));
  Transistor #(.\type ("n")) transistor_4 (.in(1'b0), .out(transistor_4_out), .gate(pull_resistor_2_node));
  Pull_Resistor #(.pull(1)) pull_resistor_3 (.node(transistor_3_out));
  Transistor #(.\type ("n")) transistor_5 (.in(1'b0), .out(transistor_5_out), .gate(transistor_3_out));
  Pull_Resistor #(.pull(1)) pull_resistor_4 (.node(transistor_5_out));
  Transistor #(.\type ("n")) transistor_6 (.in(1'b0), .out(transistor_6_out), .gate(transistor_5_out));
  Pull_Resistor #(.pull(1)) pull_resistor_5 (.node(transistor_6_out));
  Transistor #(.\type ("n")) transistor_7 (.in(1'b0), .out(O), .gate(transistor_6_out));
  Pull_Resistor #(.pull(1)) pull_resistor_6 (.node(O));
endmodule

module NOR_GATE_V2 (
  input  in_1,
  input  in_2,
  output out_3
);

  Transistor #(.\type ("n")) transistor_1 (.in(1'b0), .out(out_3), .gate(in_1));
  Pull_Resistor #(.pull(1)) pull_resistor_1 (.node(out_3));
  Transistor #(.\type ("n")) transistor_2 (.in(1'b0), .out(out_3), .gate(in_2));
endmodule

module XOR_GATE (
  input  A,
  input  B,
  output O
);

  wire and_gate_v3_1_o, and_gate_v3_2_o, not_gate_v2_1_o, not_gate_v2_2_o;

  NOT_GATE_v2 not_gate_v2_1 (.A(B), .O(not_gate_v2_1_o));
  NOT_GATE_v2 not_gate_v2_2 (.A(A), .O(not_gate_v2_2_o));
  AND_GATE_v3 and_gate_v3_1 (.A(A), .B(not_gate_v2_1_o), .O(and_gate_v3_1_o));
  AND_GATE_v3 and_gate_v3_2 (.A(not_gate_v2_2_o), .B(B), .O(and_gate_v3_2_o));
  OR_GATE_v3 or_gate_v3_1 (.A(and_gate_v3_1_o), .B(and_gate_v3_2_o), .O(O));
endmodule

module XNOR_GATE (
  input  A,
  input  B,
  output O
);

  wire nor_gate_v2_1_out_3, nor_gate_v2_2_out_3, nor_gate_v2_3_out_3;

  NOR_GATE_V2 nor_gate_v2_1 (.in_1(A), .in_2(B), .out_3(nor_gate_v2_1_out_3));
  NOR_GATE_V2 nor_gate_v2_2 (.in_1(A), .in_2(nor_gate_v2_1_out_3), .out_3(nor_gate_v2_2_out_3));
  NOR_GATE_V2 nor_gate_v2_3 (.in_1(nor_gate_v2_1_out_3), .in_2(B), .out_3(nor_gate_v2_3_out_3));
  NOR_GATE_V2 nor_gate_v2_4 (.in_1(nor_gate_v2_2_out_3), .in_2(nor_gate_v2_3_out_3), .out_3(O));
endmodule

module Halfbitaddder (
  input  A,
  input  B,
  output SUM_OUT,
  output COUT
);

  XOR_GATE xor_gate_1 (.A(A), .B(B), .O(SUM_OUT));
  AND_GATE_v3 and_gate_v3_1 (.A(A), .B(B), .O(COUT));
endmodule

module MAJ_3input (
  input  A,
  input  B,
  input  CIN,
  output O
);

  wire and_gate_v3_1_o, and_gate_v3_2_o, and_gate_v3_3_o, or_gate_v3_1_o;

  AND_GATE_v3 and_gate_v3_1 (.A(A), .B(B), .O(and_gate_v3_1_o));
  AND_GATE_v3 and_gate_v3_2 (.A(A), .B(CIN), .O(and_gate_v3_2_o));
  AND_GATE_v3 and_gate_v3_3 (.A(CIN), .B(B), .O(and_gate_v3_3_o));
  OR_GATE_v3 or_gate_v3_1 (.A(and_gate_v3_1_o), .B(and_gate_v3_2_o), .O(or_gate_v3_1_o));
  OR_GATE_v3 or_gate_v3_2 (.A(or_gate_v3_1_o), .B(and_gate_v3_3_o), .O(O));
endmodule

module ODD_3INPUT (
  input  A,
  input  B,
  input  CIN,
  output O
);

  wire xor_gate_1_o;

  XOR_GATE xor_gate_1 (.A(A), .B(B), .O(xor_gate_1_o));
  XOR_GATE xor_gate_2 (.A(xor_gate_1_o), .B(CIN), .O(O));
endmodule

module FullBitAdder (
  input  A,
  input  B,
  input  Cin,
  output Sum,
  output Cout
);

  ODD_3INPUT odd_3input_1 (.A(A), .B(B), .CIN(Cin), .O(Sum));
  MAJ_3input maj_3input_1 (.A(A), .B(B), .CIN(Cin), .O(Cout));
endmodule

module BitAdder4 (
  input  A0,
  input  B0,
  input  Cin,
  input  A1,
  input  B1,
  input  A2,
  input  B2,
  input  A3,
  input  B3,
  output S0,
  output S1,
  output S2,
  output S3,
  output COUT
);

  wire fullbitadder_1_cout, fullbitadder_2_cout, fullbitadder_3_cout;

  FullBitAdder fullbitadder_1 (.A(A0), .B(B0), .Cin(Cin), .Sum(S0), .Cout(fullbitadder_1_cout));
  FullBitAdder fullbitadder_2 (.A(A1), .B(B1), .Cin(fullbitadder_1_cout), .Sum(S1), .Cout(fullbitadder_2_cout));
  FullBitAdder fullbitadder_3 (.A(A2), .B(B2), .Cin(fullbitadder_2_cout), .Sum(S2), .Cout(fullbitadder_3_cout));
  FullBitAdder fullbitadder_4 (.A(A3), .B(B3), .Cin(fullbitadder_3_cout), .Sum(S3), .Cout(COUT));
endmodule

module bitadder4_v2 (
  input  [3:0] A,
  input  [3:0] B,
  input  CIN,
  output [3:0] sout,
  output COUT
);

  wire fullbitadder_1_cout, fullbitadder_2_cout, fullbitadder_3_cout;

  FullBitAdder fullbitadder_1 (.A(A[0]), .B(B[0]), .Cin(CIN), .Sum(sout[0]), .Cout(fullbitadder_1_cout));
  FullBitAdder fullbitadder_2 (
    .A(A[1]), .B(B[1]), .Cin(fullbitadder_1_cout), .Sum(sout[1]), .Cout(fullbitadder_2_cout));
  FullBitAdder fullbitadder_3 (
    .A(A[2]), .B(B[2]), .Cin(fullbitadder_2_cout), .Sum(sout[2]), .Cout(fullbitadder_3_cout));
  FullBitAdder fullbitadder_4 (.A(A[3]), .B(B[3]), .Cin(fullbitadder_3_cout), .Sum(sout[3]), .Cout(COUT));
endmodule

module BitAdder8 (
  input  A0,
  input  B0,
  input  CIN,
  input  A1,
  input  B1,
  input  A2,
  input  B2,
  input  A3,
  input  B3,
  input  A4,
  input  B4,
  input  A5,
  input  B5,
  input  A6,
  input  B6,
  input  A7,
  input  B7,
  output S0,
  output S1,
  output S2,
  output S3,
  output S4,
  output S5,
  output S6,
  output S7,
  output COUT
);

  wire bitadder4_1_cout;

  BitAdder4 bitadder4_1 (
    .A0(A0), .B0(B0), .Cin(CIN), .A1(A1), .B1(B1), .A2(A2), .B2(B2), .A3(A3), .B3(B3), .S0(S0), .S1(S1),
    .S2(S2), .S3(S3), .COUT(bitadder4_1_cout));
  BitAdder4 bitadder4_2 (
    .A0(A4), .B0(B4), .Cin(bitadder4_1_cout), .A1(A5), .B1(B5), .A2(A6), .B2(B6), .A3(A7), .B3(B7), .S0(S4),
    .S1(S5), .S2(S6), .S3(S7), .COUT(COUT));
endmodule

module bitadder8_v2 (
  input  [7:0] A,
  input  [7:0] B,
  input  Cin,
  output [7:0] Sout,
  output Cout
);

  wire bitadder4_v2_1_cout;

  bitadder4_v2 bitadder4_v2_1 (.A(A[3:0]), .B(B[3:0]), .CIN(Cin), .sout(Sout[3:0]), .COUT(bitadder4_v2_1_cout));
  bitadder4_v2 bitadder4_v2_2 (.A(A[7:4]), .B(B[7:4]), .CIN(bitadder4_v2_1_cout), .sout(Sout[7:4]), .COUT(Cout));
endmodule

module Multiplex_2to1 (
  input  A,
  input  B,
  input  SelectionLine,
  output O
);

  wire and_gate_v3_1_o, and_gate_v3_2_o, not_1_out;

  not not_1 (not_1_out, SelectionLine);
  AND_GATE_v3 and_gate_v3_1 (.A(A), .B(not_1_out), .O(and_gate_v3_1_o));
  OR_GATE_v3 or_gate_v3_1 (.A(and_gate_v3_1_o), .B(and_gate_v3_2_o), .O(O));
  AND_GATE_v3 and_gate_v3_2 (.A(B), .B(SelectionLine), .O(and_gate_v3_2_o));
endmodule

module Multiplex_4to1 (
  input  SelectionLine2,
  input  A,
  input  B,
  input  SelectionLine,
  input  C,
  input  D,
  output O
);

  wire multiplex_2to1_1_o, multiplex_2to1_2_o;

  Multiplex_2to1 multiplex_2to1_1 (.A(SelectionLine), .B(A), .SelectionLine(B), .O(multiplex_2to1_1_o));
  Multiplex_2to1 multiplex_2to1_2 (.A(SelectionLine), .B(C), .SelectionLine(D), .O(multiplex_2to1_2_o));
  Multiplex_2to1 multiplex_2to1_3 (
    .A(SelectionLine2), .B(multiplex_2to1_1_o), .SelectionLine(multiplex_2to1_2_o), .O(O));
endmodule

module FourBitAND (
  input  [3:0] A,
  input  [3:0] B,
  output [3:0] O
);

  AND_GATE_v3 and_gate_v3_1 (.A(A[0]), .B(B[0]), .O(O[0]));
  AND_GATE_v3 and_gate_v3_2 (.A(A[1]), .B(B[1]), .O(O[1]));
  AND_GATE_v3 and_gate_v3_3 (.A(A[2]), .B(B[2]), .O(O[2]));
  AND_GATE_v3 and_gate_v3_4 (.A(A[3]), .B(B[3]), .O(O[3]));
endmodule

module EightBitAND (
  input  [7:0] A,
  input  [7:0] B,
  output [7:0] O
);

  FourBitAND fourbitand_1 (.A(A[3:0]), .B(B[3:0]), .O(O[3:0]));
  FourBitAND fourbitand_2 (.A(A[7:4]), .B(B[7:4]), .O(O[7:4]));
endmodule

module FourBitXOR (
  input  [3:0] A,
  input  [3:0] B,
  output [3:0] O
);

  XOR_GATE xor_gate_1 (.A(A[0]), .B(B[0]), .O(O[0]));
  XOR_GATE xor_gate_2 (.A(A[1]), .B(B[1]), .O(O[1]));
  XOR_GATE xor_gate_3 (.A(A[2]), .B(B[2]), .O(O[2]));
  XOR_GATE xor_gate_4 (.A(A[3]), .B(B[3]), .O(O[3]));
endmodule

module EightBitXOR (
  input  [7:0] A,
  input  [7:0] B,
  output [7:0] O
);

  FourBitXOR fourbitxor_1 (.A(A[3:0]), .B(B[3:0]), .O(O[3:0]));
  FourBitXOR fourbitxor_2 (.A(A[7:4]), .B(B[7:4]), .O(O[7:4]));
endmodule

module bitsubtractor8 (
  input  [7:0] A,
  input  [7:0] B,
  output [7:0] Sout,
  output Cout
);

  wire [7:0] bit8not_1_b;

  bit8NOT bit8not_1 (.A(B), .B(bit8not_1_b));
  bitadder8_v2 bitadder8_v2_1 (.A(A), .B(bit8not_1_b), .Cin(1'b1), .Sout(Sout), .Cout(Cout));
endmodule

module bit8NOT (
  input  [7:0] A,
  output [7:0] B
);

  NOT_GATE_v2 not_gate_v2_1 (.A(A[0]), .O(B[0]));
  NOT_GATE_v2 not_gate_v2_2 (.A(A[1]), .O(B[1]));
  NOT_GATE_v2 not_gate_v2_3 (.A(A[2]), .O(B[2]));
  NOT_GATE_v2 not_gate_v2_4 (.A(A[3]), .O(B[3]));
  NOT_GATE_v2 not_gate_v2_5 (.A(A[4]), .O(B[4]));
  NOT_GATE_v2 not_gate_v2_6 (.A(A[5]), .O(B[5]));
  NOT_GATE_v2 not_gate_v2_7 (.A(A[6]), .O(B[6]));
  NOT_GATE_v2 not_gate_v2_8 (.A(A[7]), .O(B[7]));
endmodule

module Left_Shifter (
  input  [7:0] A,
  output [7:0] O
);


  assign O = {A[6:0], 1'b0};
endmodule

module Right_Shifter (
  input  [7:0] A,
  output [7:0] O
);


  assign O = {1'b0, A[7:1]};
endmodule

module OneHotMux_1to6 (
  input  ADD_BIT,
  input  SEL_ADD,
  input  SUB_BIT,
  input  SEL_SUB,
  input  AND_BIT,
  input  SEL_AND,
  input  XOR_BIT,
  input  SEL_XOR,
  input  LShift_BIT,
  input  SEL_LShift,
  input  RShift_BIT,
  input  SEL_RShift,
  output O
);

  wire and_1_out, and_2_out, and_3_out, and_4_out, and_5_out, and_6_out, or_1_out, or_2_out, or_3_out,
       or_4_out;

  and and_1 (and_1_out, ADD_BIT, SEL_ADD);
  and and_2 (and_2_out, SUB_BIT, SEL_SUB);
  and and_3 (and_3_out, AND_BIT, SEL_AND);
  and and_4 (and_4_out, XOR_BIT, SEL_XOR);
  and and_5 (and_5_out, LShift_BIT, SEL_LShift);
  and and_6 (and_6_out, RShift_BIT, SEL_RShift);
  or or_1 (or_1_out, and_1_out, and_2_out);
  or or_2 (or_2_out, or_1_out, and_3_out);
  or or_3 (or_3_out, or_2_out, and_4_out);
  or or_4 (or_4_out, or_3_out, and_5_out);
  or or_5 (O, or_4_out, and_6_out);
endmodule

module Onehotmux_1to6_8bit (
  input  [7:0] ADD_8BIT,
  input  SEL_ADD,
  input  [7:0] SUB_8BIT,
  input  SEL_SUB,
  input  [7:0] AND_8BIT,
  input  SEL_AND,
  input  [7:0] XOR_8BIT,
  input  SEL_XOR,
  input  [7:0] LSHIFT_8BIT,
  input  SEL_LSHIFT,
  input  [7:0] RSHIFT_8BIT,
  input  SEL_RSHIFT,
  output [7:0] O
);

  OneHotMux_1to6 onehotmux_1to6_1 (
    .ADD_BIT(ADD_8BIT[1]), .SEL_ADD(SEL_ADD), .SUB_BIT(SUB_8BIT[1]), .SEL_SUB(SEL_SUB),
    .AND_BIT(AND_8BIT[1]), .SEL_AND(SEL_AND), .XOR_BIT(XOR_8BIT[1]), .SEL_XOR(SEL_XOR),
    .LShift_BIT(LSHIFT_8BIT[1]), .SEL_LShift(SEL_LSHIFT), .RShift_BIT(RSHIFT_8BIT[1]),
    .SEL_RShift(SEL_RSHIFT), .O(O[1]));
  OneHotMux_1to6 onehotmux_1to6_2 (
    .ADD_BIT(ADD_8BIT[3]), .SEL_ADD(SEL_ADD), .SUB_BIT(SUB_8BIT[3]), .SEL_SUB(SEL_SUB),
    .AND_BIT(AND_8BIT[3]), .SEL_AND(SEL_AND), .XOR_BIT(XOR_8BIT[3]), .SEL_XOR(SEL_XOR),
    .LShift_BIT(LSHIFT_8BIT[3]), .SEL_LShift(SEL_LSHIFT), .RShift_BIT(RSHIFT_8BIT[3]),
    .SEL_RShift(SEL_RSHIFT), .O(O[3]));
  OneHotMux_1to6 onehotmux_1to6_3 (
    .ADD_BIT(ADD_8BIT[5]), .SEL_ADD(SEL_ADD), .SUB_BIT(SUB_8BIT[5]), .SEL_SUB(SEL_SUB),
    .AND_BIT(AND_8BIT[5]), .SEL_AND(SEL_AND), .XOR_BIT(XOR_8BIT[5]), .SEL_XOR(SEL_XOR),
    .LShift_BIT(LSHIFT_8BIT[5]), .SEL_LShift(SEL_LSHIFT), .RShift_BIT(RSHIFT_8BIT[5]),
    .SEL_RShift(SEL_RSHIFT), .O(O[5]));
  OneHotMux_1to6 onehotmux_1to6_4 (
    .ADD_BIT(ADD_8BIT[7]), .SEL_ADD(SEL_ADD), .SUB_BIT(SUB_8BIT[7]), .SEL_SUB(SEL_SUB),
    .AND_BIT(AND_8BIT[7]), .SEL_AND(SEL_AND), .XOR_BIT(XOR_8BIT[7]), .SEL_XOR(SEL_XOR),
    .LShift_BIT(LSHIFT_8BIT[7]), .SEL_LShift(SEL_LSHIFT), .RShift_BIT(RSHIFT_8BIT[7]),
    .SEL_RShift(SEL_RSHIFT), .O(O[7]));
  OneHotMux_1to6 onehotmux_1to6_5 (
    .ADD_BIT(ADD_8BIT[0]), .SEL_ADD(SEL_ADD), .SUB_BIT(SUB_8BIT[0]), .SEL_SUB(SEL_SUB),
    .AND_BIT(AND_8BIT[0]), .SEL_AND(SEL_AND), .XOR_BIT(XOR_8BIT[0]), .SEL_XOR(SEL_XOR),
    .LShift_BIT(LSHIFT_8BIT[0]), .SEL_LShift(SEL_LSHIFT), .RShift_BIT(RSHIFT_8BIT[0]),
    .SEL_RShift(SEL_RSHIFT), .O(O[0]));
  OneHotMux_1to6 onehotmux_1to6_6 (
    .ADD_BIT(ADD_8BIT[2]), .SEL_ADD(SEL_ADD), .SUB_BIT(SUB_8BIT[2]), .SEL_SUB(SEL_SUB),
    .AND_BIT(AND_8BIT[2]), .SEL_AND(SEL_AND), .XOR_BIT(XOR_8BIT[2]), .SEL_XOR(SEL_XOR),
    .LShift_BIT(LSHIFT_8BIT[2]), .SEL_LShift(SEL_LSHIFT), .RShift_BIT(RSHIFT_8BIT[2]),
    .SEL_RShift(SEL_RSHIFT), .O(O[2]));
  OneHotMux_1to6 onehotmux_1to6_7 (
    .ADD_BIT(ADD_8BIT[4]), .SEL_ADD(SEL_ADD), .SUB_BIT(SUB_8BIT[4]), .SEL_SUB(SEL_SUB),
    .AND_BIT(AND_8BIT[4]), .SEL_AND(SEL_AND), .XOR_BIT(XOR_8BIT[4]), .SEL_XOR(SEL_XOR),
    .LShift_BIT(LSHIFT_8BIT[4]), .SEL_LShift(SEL_LSHIFT), .RShift_BIT(RSHIFT_8BIT[4]),
    .SEL_RShift(SEL_RSHIFT), .O(O[4]));
  OneHotMux_1to6 onehotmux_1to6_8 (
    .ADD_BIT(ADD_8BIT[6]), .SEL_ADD(SEL_ADD), .SUB_BIT(SUB_8BIT[6]), .SEL_SUB(SEL_SUB),
    .AND_BIT(AND_8BIT[6]), .SEL_AND(SEL_AND), .XOR_BIT(XOR_8BIT[6]), .SEL_XOR(SEL_XOR),
    .LShift_BIT(LSHIFT_8BIT[6]), .SEL_LShift(SEL_LSHIFT), .RShift_BIT(RSHIFT_8BIT[6]),
    .SEL_RShift(SEL_RSHIFT), .O(O[6]));
endmodule

module Decoder_3to8 (
  input  OP_0,
  input  OP_1,
  input  OP_2,
  output D0,
  output D1,
  output D2,
  output D3,
  output D4,
  output D5,
  output D6,
  output D7
);

  wire not_1_out, not_2_out, not_3_out;

  not not_1 (not_1_out, OP_0);
  not not_2 (not_2_out, OP_1);
  not not_3 (not_3_out, OP_2);
  AND_GATE_3INPUT and_gate_3input_1 (.A(not_1_out), .B(not_2_out), .C(not_3_out), .O(D0));
  AND_GATE_3INPUT and_gate_3input_2 (.A(OP_0), .B(not_2_out), .C(not_3_out), .O(D1));
  AND_GATE_3INPUT and_gate_3input_3 (.A(not_1_out), .B(OP_1), .C(not_3_out), .O(D2));
  AND_GATE_3INPUT and_gate_3input_4 (.A(OP_0), .B(OP_1), .C(not_3_out), .O(D3));
  AND_GATE_3INPUT and_gate_3input_5 (.A(not_1_out), .B(not_2_out), .C(OP_2), .O(D4));
  AND_GATE_3INPUT and_gate_3input_6 (.A(OP_0), .B(not_2_out), .C(OP_2), .O(D5));
  AND_GATE_3INPUT and_gate_3input_7 (.A(not_1_out), .B(OP_1), .C(OP_2), .O(D6));
  AND_GATE_3INPUT and_gate_3input_8 (.A(OP_0), .B(OP_1), .C(OP_2), .O(D7));
endmodule

module AND_GATE_3INPUT (
  input  A,
  input  B,
  input  C,
  output O
);

  wire and_1_out;

  and and_1 (and_1_out, A, B);
  and and_2 (O, and_1_out, C);
endmodule

module ALU_8Bit_With_Decoder (
  input  [7:0] A,
  input  [7:0] B,
  input  [2:0] OP_CODE,
  output [7:0] ALU_OUT,
  output COUT
);

  wire and_1_out, and_2_out, bitadder8_v2_1_cout, bitsubtractor8_1_cout, decoder_3to8_1_d0,
       decoder_3to8_1_d1, decoder_3to8_1_d2, decoder_3to8_1_d3, decoder_3to8_1_d4, decoder_3to8_1_d5;
  wire [7:0] bitadder8_v2_1_sout, bitsubtractor8_1_sout, eightbitand_1_o, eightbitxor_1_o, left_shifter_1_o,
       right_shifter_1_o;

  Decoder_3to8 decoder_3to8_1 (
    .OP_0(OP_CODE[0]), .OP_1(OP_CODE[1]), .OP_2(OP_CODE[2]), .D0(decoder_3to8_1_d0), .D1(decoder_3to8_1_d1),
    .D2(decoder_3to8_1_d2), .D3(decoder_3to8_1_d3), .D4(decoder_3to8_1_d4), .D5(decoder_3to8_1_d5));  // open: D6, D7
  bitadder8_v2 bitadder8_v2_1 (.A(A), .B(B), .Cin(1'b0), .Sout(bitadder8_v2_1_sout), .Cout(bitadder8_v2_1_cout));
  bitsubtractor8 bitsubtractor8_1 (.A(A), .B(B), .Sout(bitsubtractor8_1_sout), .Cout(bitsubtractor8_1_cout));
  EightBitAND eightbitand_1 (.A(A), .B(B), .O(eightbitand_1_o));
  EightBitXOR eightbitxor_1 (.A(A), .B(B), .O(eightbitxor_1_o));
  Left_Shifter left_shifter_1 (.A(A), .O(left_shifter_1_o));
  Right_Shifter right_shifter_1 (.A(A), .O(right_shifter_1_o));
  Onehotmux_1to6_8bit onehotmux_1to6_8bit_1 (
    .ADD_8BIT(bitadder8_v2_1_sout), .SEL_ADD(decoder_3to8_1_d0), .SUB_8BIT(bitsubtractor8_1_sout),
    .SEL_SUB(decoder_3to8_1_d1), .AND_8BIT(eightbitand_1_o), .SEL_AND(decoder_3to8_1_d2),
    .XOR_8BIT(eightbitxor_1_o), .SEL_XOR(decoder_3to8_1_d3), .LSHIFT_8BIT(left_shifter_1_o),
    .SEL_LSHIFT(decoder_3to8_1_d4), .RSHIFT_8BIT(right_shifter_1_o), .SEL_RSHIFT(decoder_3to8_1_d5),
    .O(ALU_OUT));
  and and_1 (and_1_out, bitadder8_v2_1_cout, decoder_3to8_1_d0);
  and and_2 (and_2_out, bitsubtractor8_1_cout, decoder_3to8_1_d1);
  or or_1 (COUT, and_1_out, and_2_out);
endmodule

module Demux_3to8 (
  input  OP_0,
  input  OP_1,
  input  OP_2,
  input  X,
  output Y0,
  output Y1,
  output Y2,
  output Y3,
  output Y4,
  output Y5,
  output Y6,
  output Y7
);

  wire decoder_3to8_1_d0, decoder_3to8_1_d1, decoder_3to8_1_d2, decoder_3to8_1_d3, decoder_3to8_1_d4,
       decoder_3to8_1_d5, decoder_3to8_1_d6, decoder_3to8_1_d7;

  Decoder_3to8 decoder_3to8_1 (
    .OP_0(OP_0), .OP_1(OP_1), .OP_2(OP_2), .D0(decoder_3to8_1_d0), .D1(decoder_3to8_1_d1),
    .D2(decoder_3to8_1_d2), .D3(decoder_3to8_1_d3), .D4(decoder_3to8_1_d4), .D5(decoder_3to8_1_d5),
    .D6(decoder_3to8_1_d6), .D7(decoder_3to8_1_d7));
  and and_1 (Y0, decoder_3to8_1_d0, X);
  and and_2 (Y1, decoder_3to8_1_d1, X);
  and and_3 (Y2, decoder_3to8_1_d2, X);
  and and_4 (Y3, decoder_3to8_1_d3, X);
  and and_5 (Y4, decoder_3to8_1_d4, X);
  and and_6 (Y5, decoder_3to8_1_d5, X);
  and and_7 (Y6, decoder_3to8_1_d6, X);
  and and_8 (Y7, decoder_3to8_1_d7, X);
endmodule

module DecoderDemux_3to8bit (
  input  OP_0,
  input  OP_1,
  input  OP_2,
  input  X,
  output D0,
  output D1,
  output D2,
  output D3,
  output D4,
  output D5,
  output D6,
  output D7,
  output Y0,
  output Y1,
  output Y2,
  output Y3,
  output Y4,
  output Y5,
  output Y6,
  output Y7
);

  Decoder_3to8 decoder_3to8_1 (
    .OP_0(OP_0), .OP_1(OP_1), .OP_2(OP_2), .D0(D0), .D1(D1), .D2(D2), .D3(D3), .D4(D4), .D5(D5), .D6(D6),
    .D7(D7));
  Demux_3to8 demux_3to8_1 (
    .OP_0(OP_0), .OP_1(OP_1), .OP_2(OP_2), .X(X), .Y0(Y0), .Y1(Y1), .Y2(Y2), .Y3(Y3), .Y4(Y4), .Y5(Y5),
    .Y6(Y6), .Y7(Y7));
endmodule

module ALU_8BIT_V2 (
  input  [7:0] A,
  input  [7:0] B,
  input  SEL_ADD,
  input  SEL_SUB,
  input  SEL_AND,
  input  SEL_XOR,
  input  SEL_LShift,
  input  SEL_RShift,
  output [7:0] ALU_OUT,
  output COUT
);

  wire and_1_out, and_2_out, bitadder8_v2_1_cout, bitsubtractor8_1_cout;
  wire [7:0] bitadder8_v2_1_sout, bitsubtractor8_1_sout, eightbitand_1_o, eightbitxor_1_o, left_shifter_1_o,
       right_shifter_1_o;

  bitadder8_v2 bitadder8_v2_1 (.A(A), .B(B), .Cin(1'b0), .Sout(bitadder8_v2_1_sout), .Cout(bitadder8_v2_1_cout));
  bitsubtractor8 bitsubtractor8_1 (.A(A), .B(B), .Sout(bitsubtractor8_1_sout), .Cout(bitsubtractor8_1_cout));
  EightBitAND eightbitand_1 (.A(A), .B(B), .O(eightbitand_1_o));
  EightBitXOR eightbitxor_1 (.A(A), .B(B), .O(eightbitxor_1_o));
  Left_Shifter left_shifter_1 (.A(A), .O(left_shifter_1_o));
  Right_Shifter right_shifter_1 (.A(A), .O(right_shifter_1_o));
  Onehotmux_1to6_8bit onehotmux_1to6_8bit_1 (
    .ADD_8BIT(bitadder8_v2_1_sout), .SEL_ADD(SEL_ADD), .SUB_8BIT(bitsubtractor8_1_sout), .SEL_SUB(SEL_SUB),
    .AND_8BIT(eightbitand_1_o), .SEL_AND(SEL_AND), .XOR_8BIT(eightbitxor_1_o), .SEL_XOR(SEL_XOR),
    .LSHIFT_8BIT(left_shifter_1_o), .SEL_LSHIFT(SEL_LShift), .RSHIFT_8BIT(right_shifter_1_o),
    .SEL_RSHIFT(SEL_RShift), .O(ALU_OUT));
  and and_1 (and_1_out, bitadder8_v2_1_cout, SEL_ADD);
  and and_2 (and_2_out, bitsubtractor8_1_cout, SEL_SUB);
  or or_1 (COUT, and_1_out, and_2_out);
endmodule

module SR_LATCH (
  input  S,
  input  R,
  output Qbar,
  output Q
);

  nor nor_1 (Qbar, S, Q);
  nor nor_2 (Q, R, Qbar);
endmodule

module Memory_bit (
  input  IN_PUT,
  input  write,
  input  CLOCK,
  output OUT_PUT
);

  wire and_1_out, and_2_out, not_1_out;

  not not_1 (not_1_out, IN_PUT);
  and and_1 (and_1_out, IN_PUT, write);
  and and_2 (and_2_out, not_1_out, write);
  S_R_Flip_Flop s_r_ff_1 (.S(and_1_out), .R(and_2_out), .clk(CLOCK), .Q(OUT_PUT));  // open: reset, Qn, preset
endmodule

module Register_4Bit (
  input  [3:0] IN_PUT,
  input  WRITE,
  input  CLOCK,
  output [3:0] out_4
);

  Memory_bit memory_bit_1 (.IN_PUT(IN_PUT[0]), .write(WRITE), .CLOCK(CLOCK), .OUT_PUT(out_4[0]));
  Memory_bit memory_bit_2 (.IN_PUT(IN_PUT[1]), .write(WRITE), .CLOCK(CLOCK), .OUT_PUT(out_4[1]));
  Memory_bit memory_bit_3 (.IN_PUT(IN_PUT[2]), .write(WRITE), .CLOCK(CLOCK), .OUT_PUT(out_4[2]));
  Memory_bit memory_bit_4 (.IN_PUT(IN_PUT[3]), .write(WRITE), .CLOCK(CLOCK), .OUT_PUT(out_4[3]));
endmodule

module Register_8Bit (
  input  [7:0] IN_PUT,
  input  WRITE,
  input  CLOCK,
  output [7:0] O
);

  Register_4Bit register_4bit_1 (.IN_PUT(IN_PUT[3:0]), .WRITE(WRITE), .CLOCK(CLOCK), .out_4(O[3:0]));
  Register_4Bit register_4bit_2 (.IN_PUT(IN_PUT[7:4]), .WRITE(WRITE), .CLOCK(CLOCK), .out_4(O[7:4]));
endmodule

module Decoder_4to16 (
  input  A0,
  input  A1,
  input  A2,
  input  A3,
  output D0,
  output D1,
  output D2,
  output D3,
  output D4,
  output D5,
  output D6,
  output D7,
  output D8,
  output D9,
  output D10,
  output D11,
  output D12,
  output D13,
  output D14,
  output D15
);

  wire decoder_3to8_1_d0, decoder_3to8_1_d1, decoder_3to8_1_d2, decoder_3to8_1_d3, decoder_3to8_1_d4,
       decoder_3to8_1_d5, decoder_3to8_1_d6, decoder_3to8_1_d7, decoder_3to8_2_d0, decoder_3to8_2_d1,
       decoder_3to8_2_d2, decoder_3to8_2_d3, decoder_3to8_2_d4, decoder_3to8_2_d5, decoder_3to8_2_d6,
       decoder_3to8_2_d7, not_1_out;

  not not_1 (not_1_out, A3);
  Decoder_3to8 decoder_3to8_1 (
    .OP_0(A0), .OP_1(A1), .OP_2(A2), .D0(decoder_3to8_1_d0), .D1(decoder_3to8_1_d1), .D2(decoder_3to8_1_d2),
    .D3(decoder_3to8_1_d3), .D4(decoder_3to8_1_d4), .D5(decoder_3to8_1_d5), .D6(decoder_3to8_1_d6),
    .D7(decoder_3to8_1_d7));
  Decoder_3to8 decoder_3to8_2 (
    .OP_0(A0), .OP_1(A1), .OP_2(A2), .D0(decoder_3to8_2_d0), .D1(decoder_3to8_2_d1), .D2(decoder_3to8_2_d2),
    .D3(decoder_3to8_2_d3), .D4(decoder_3to8_2_d4), .D5(decoder_3to8_2_d5), .D6(decoder_3to8_2_d6),
    .D7(decoder_3to8_2_d7));
  and and_1 (D0, decoder_3to8_1_d0, not_1_out);
  and and_2 (D1, decoder_3to8_1_d1, not_1_out);
  and and_3 (D2, decoder_3to8_1_d2, not_1_out);
  and and_4 (D3, decoder_3to8_1_d3, not_1_out);
  and and_5 (D4, decoder_3to8_1_d4, not_1_out);
  and and_6 (D5, decoder_3to8_1_d5, not_1_out);
  and and_7 (D6, decoder_3to8_1_d6, not_1_out);
  and and_8 (D7, decoder_3to8_1_d7, not_1_out);
  and and_9 (D8, decoder_3to8_2_d0, A3);
  and and_10 (D9, decoder_3to8_2_d1, A3);
  and and_11 (D10, decoder_3to8_2_d2, A3);
  and and_12 (D11, decoder_3to8_2_d3, A3);
  and and_13 (D12, decoder_3to8_2_d4, A3);
  and and_14 (D13, decoder_3to8_2_d5, A3);
  and and_15 (D14, decoder_3to8_2_d6, A3);
  and and_16 (D15, decoder_3to8_2_d7, A3);
endmodule

module Demux_4to16 (
  input  A0,
  input  A1,
  input  A2,
  input  A3,
  input  X,
  output Y0,
  output Y1,
  output Y2,
  output Y3,
  output Y4,
  output Y5,
  output Y6,
  output Y7,
  output Y8,
  output Y9,
  output Y10,
  output Y11,
  output Y12,
  output Y13,
  output Y14,
  output Y15
);

  wire decoder_4to16_1_d0, decoder_4to16_1_d1, decoder_4to16_1_d2, decoder_4to16_1_d3, decoder_4to16_1_d4,
       decoder_4to16_1_d5, decoder_4to16_1_d6, decoder_4to16_1_d7, decoder_4to16_1_d8, decoder_4to16_1_d9,
       decoder_4to16_1_d10, decoder_4to16_1_d11, decoder_4to16_1_d12, decoder_4to16_1_d13,
       decoder_4to16_1_d14, decoder_4to16_1_d15;

  Decoder_4to16 decoder_4to16_1 (
    .A0(A0), .A1(A1), .A2(A2), .A3(A3), .D0(decoder_4to16_1_d0), .D1(decoder_4to16_1_d1),
    .D2(decoder_4to16_1_d2), .D3(decoder_4to16_1_d3), .D4(decoder_4to16_1_d4), .D5(decoder_4to16_1_d5),
    .D6(decoder_4to16_1_d6), .D7(decoder_4to16_1_d7), .D8(decoder_4to16_1_d8), .D9(decoder_4to16_1_d9),
    .D10(decoder_4to16_1_d10), .D11(decoder_4to16_1_d11), .D12(decoder_4to16_1_d12),
    .D13(decoder_4to16_1_d13), .D14(decoder_4to16_1_d14), .D15(decoder_4to16_1_d15));
  and and_1 (Y0, decoder_4to16_1_d0, X);
  and and_2 (Y1, decoder_4to16_1_d1, X);
  and and_3 (Y2, decoder_4to16_1_d2, X);
  and and_4 (Y3, decoder_4to16_1_d3, X);
  and and_5 (Y4, decoder_4to16_1_d4, X);
  and and_6 (Y5, decoder_4to16_1_d5, X);
  and and_7 (Y6, decoder_4to16_1_d6, X);
  and and_8 (Y7, decoder_4to16_1_d7, X);
  and and_9 (Y8, decoder_4to16_1_d8, X);
  and and_10 (Y9, decoder_4to16_1_d9, X);
  and and_11 (Y10, decoder_4to16_1_d10, X);
  and and_12 (Y11, decoder_4to16_1_d11, X);
  and and_13 (Y12, decoder_4to16_1_d12, X);
  and and_14 (Y13, decoder_4to16_1_d13, X);
  and and_15 (Y14, decoder_4to16_1_d14, X);
  and and_16 (Y15, decoder_4to16_1_d15, X);
endmodule

module DecoderDemux_4to16 (
  input  A0,
  input  A1,
  input  A2,
  input  A3,
  input  X,
  output D0,
  output D1,
  output D2,
  output D3,
  output D4,
  output D5,
  output D6,
  output D7,
  output D8,
  output D9,
  output D10,
  output D11,
  output D12,
  output D13,
  output D14,
  output D15,
  output Y0,
  output Y1,
  output Y2,
  output Y3,
  output Y4,
  output Y5,
  output Y6,
  output Y7,
  output Y8,
  output Y9,
  output Y10,
  output Y11,
  output Y12,
  output Y13,
  output Y14,
  output Y15
);

  Decoder_4to16 decoder_4to16_1 (
    .A0(A0), .A1(A1), .A2(A2), .A3(A3), .D0(D0), .D1(D1), .D2(D2), .D3(D3), .D4(D4), .D5(D5), .D6(D6),
    .D7(D7), .D8(D8), .D9(D9), .D10(D10), .D11(D11), .D12(D12), .D13(D13), .D14(D14), .D15(D15));
  Demux_4to16 demux_4to16_1 (
    .A0(A0), .A1(A1), .A2(A2), .A3(A3), .X(X), .Y0(Y0), .Y1(Y1), .Y2(Y2), .Y3(Y3), .Y4(Y4), .Y5(Y5), .Y6(Y6),
    .Y7(Y7), .Y8(Y8), .Y9(Y9), .Y10(Y10), .Y11(Y11), .Y12(Y12), .Y13(Y13), .Y14(Y14), .Y15(Y15));
endmodule

module Onehotmux_16to1_1bit (
  input  IN0,
  input  SEL_0,
  input  IN1,
  input  SEL_1,
  input  IN2,
  input  SEL_2,
  input  IN3,
  input  SEL_3,
  input  IN4,
  input  SEL_4,
  input  IN5,
  input  SEL_5,
  input  IN6,
  input  SEL_6,
  input  IN7,
  input  SEL_7,
  input  IN8,
  input  SEL_8,
  input  IN9,
  input  SEL_9,
  input  IN10,
  input  SEL_10,
  input  IN11,
  input  SEL_11,
  input  IN12,
  input  SEL_12,
  input  IN13,
  input  SEL_13,
  input  IN14,
  input  SEL_14,
  input  IN15,
  input  SEL_15,
  output O
);

  wire and_1_out, and_2_out, and_3_out, and_4_out, and_5_out, and_6_out, and_7_out, and_8_out, and_9_out,
       and_10_out, and_11_out, and_12_out, and_13_out, and_14_out, and_15_out, and_16_out, or_1_out,
       or_2_out, or_3_out, or_4_out, or_5_out, or_6_out, or_7_out, or_8_out, or_9_out, or_10_out, or_11_out,
       or_12_out, or_13_out, or_14_out;

  and and_1 (and_1_out, IN0, SEL_0);
  and and_2 (and_2_out, IN1, SEL_1);
  and and_3 (and_3_out, IN2, SEL_2);
  and and_4 (and_4_out, IN3, SEL_3);
  and and_5 (and_5_out, IN4, SEL_4);
  and and_6 (and_6_out, IN5, SEL_5);
  and and_7 (and_7_out, IN6, SEL_6);
  and and_8 (and_8_out, IN7, SEL_7);
  and and_9 (and_9_out, IN8, SEL_8);
  and and_10 (and_10_out, IN9, SEL_9);
  and and_11 (and_11_out, IN10, SEL_10);
  and and_12 (and_12_out, IN11, SEL_11);
  and and_13 (and_13_out, IN12, SEL_12);
  and and_14 (and_14_out, IN13, SEL_13);
  and and_15 (and_15_out, IN14, SEL_14);
  and and_16 (and_16_out, IN15, SEL_15);
  or or_1 (or_1_out, and_1_out, and_2_out);
  or or_2 (or_2_out, or_1_out, and_3_out);
  or or_3 (or_3_out, or_2_out, and_4_out);
  or or_4 (or_4_out, or_3_out, and_5_out);
  or or_5 (or_5_out, or_4_out, and_6_out);
  or or_6 (or_6_out, or_5_out, and_7_out);
  or or_7 (or_7_out, or_6_out, and_8_out);
  or or_8 (or_8_out, or_7_out, and_9_out);
  or or_9 (or_9_out, or_8_out, and_10_out);
  or or_10 (or_10_out, or_9_out, and_11_out);
  or or_11 (or_11_out, or_10_out, and_12_out);
  or or_12 (or_12_out, or_11_out, and_13_out);
  or or_13 (or_13_out, or_12_out, and_14_out);
  or or_14 (or_14_out, or_13_out, and_15_out);
  or or_15 (O, or_14_out, and_16_out);
endmodule

module Onehotmux_16to1_2bit (
  input  [1:0] IN0,
  input  SEL_0,
  input  [1:0] IN1,
  input  SEL_1,
  input  [1:0] IN2,
  input  SEL_2,
  input  [1:0] IN3,
  input  SEL_3,
  input  [1:0] IN4,
  input  SEL_4,
  input  [1:0] IN5,
  input  SEL_5,
  input  [1:0] IN6,
  input  SEL_6,
  input  [1:0] IN7,
  input  SEL_7,
  input  [1:0] IN8,
  input  SEL_8,
  input  [1:0] IN9,
  input  SEL_9,
  input  [1:0] IN10,
  input  SEL_10,
  input  [1:0] IN11,
  input  SEL_11,
  input  [1:0] IN12,
  input  SEL_12,
  input  [1:0] IN13,
  input  SEL_13,
  input  [1:0] IN14,
  input  SEL_14,
  input  [1:0] IN15,
  input  SEL_15,
  output [1:0] out_33
);

  Onehotmux_16to1_1bit onehotmux_16to1_1bit_1 (
    .IN0(IN0[0]), .SEL_0(SEL_0), .IN1(IN1[0]), .SEL_1(SEL_1), .IN2(IN2[0]), .SEL_2(SEL_2), .IN3(IN3[0]),
    .SEL_3(SEL_3), .IN4(IN4[0]), .SEL_4(SEL_4), .IN5(IN5[0]), .SEL_5(SEL_5), .IN6(IN6[0]), .SEL_6(SEL_6),
    .IN7(IN7[0]), .SEL_7(SEL_7), .IN8(IN8[0]), .SEL_8(SEL_8), .IN9(IN9[0]), .SEL_9(SEL_9), .IN10(IN10[0]),
    .SEL_10(SEL_10), .IN11(IN11[0]), .SEL_11(SEL_11), .IN12(IN12[0]), .SEL_12(SEL_12), .IN13(IN13[0]),
    .SEL_13(SEL_13), .IN14(IN14[0]), .SEL_14(SEL_14), .IN15(IN15[0]), .SEL_15(SEL_15), .O(out_33[0]));
  Onehotmux_16to1_1bit onehotmux_16to1_1bit_2 (
    .IN0(IN0[1]), .SEL_0(SEL_0), .IN1(IN1[1]), .SEL_1(SEL_1), .IN2(IN2[1]), .SEL_2(SEL_2), .IN3(IN3[1]),
    .SEL_3(SEL_3), .IN4(IN4[1]), .SEL_4(SEL_4), .IN5(IN5[1]), .SEL_5(SEL_5), .IN6(IN6[1]), .SEL_6(SEL_6),
    .IN7(IN7[1]), .SEL_7(SEL_7), .IN8(IN8[1]), .SEL_8(SEL_8), .IN9(IN9[1]), .SEL_9(SEL_9), .IN10(IN10[1]),
    .SEL_10(SEL_10), .IN11(IN11[1]), .SEL_11(SEL_11), .IN12(IN12[1]), .SEL_12(SEL_12), .IN13(IN13[1]),
    .SEL_13(SEL_13), .IN14(IN14[1]), .SEL_14(SEL_14), .IN15(IN15[1]), .SEL_15(SEL_15), .O(out_33[1]));
endmodule

module Onehotmux_16to1_4bit (
  input  [3:0] IN0,
  input  SEL_0,
  input  [3:0] IN1,
  input  SEL_1,
  input  [3:0] IN2,
  input  SEL_2,
  input  [3:0] IN3,
  input  SEL_3,
  input  [3:0] IN4,
  input  SEL_4,
  input  [3:0] IN5,
  input  SEL_5,
  input  [3:0] IN6,
  input  SEL_6,
  input  [3:0] IN7,
  input  SEL_7,
  input  [3:0] IN8,
  input  SEL_8,
  input  [3:0] IN9,
  input  SEL_9,
  input  [3:0] IN10,
  input  SEL_10,
  input  [3:0] IN11,
  input  SEL_11,
  input  [3:0] IN12,
  input  SEL_12,
  input  [3:0] IN13,
  input  SEL_13,
  input  [3:0] IN14,
  input  SEL_14,
  input  [3:0] IN15,
  input  SEL_15,
  output [3:0] O
);

  Onehotmux_16to1_2bit onehotmux_16to1_2bit_1 (
    .IN0(IN0[1:0]), .SEL_0(SEL_0), .IN1(IN1[1:0]), .SEL_1(SEL_1), .IN2(IN2[1:0]), .SEL_2(SEL_2),
    .IN3(IN3[1:0]), .SEL_3(SEL_3), .IN4(IN4[1:0]), .SEL_4(SEL_4), .IN5(IN5[1:0]), .SEL_5(SEL_5),
    .IN6(IN6[1:0]), .SEL_6(SEL_6), .IN7(IN7[1:0]), .SEL_7(SEL_7), .IN8(IN8[1:0]), .SEL_8(SEL_8),
    .IN9(IN9[1:0]), .SEL_9(SEL_9), .IN10(IN10[1:0]), .SEL_10(SEL_10), .IN11(IN11[1:0]), .SEL_11(SEL_11),
    .IN12(IN12[1:0]), .SEL_12(SEL_12), .IN13(IN13[1:0]), .SEL_13(SEL_13), .IN14(IN14[1:0]), .SEL_14(SEL_14),
    .IN15(IN15[1:0]), .SEL_15(SEL_15), .out_33(O[1:0]));
  Onehotmux_16to1_2bit onehotmux_16to1_2bit_2 (
    .IN0(IN0[3:2]), .SEL_0(SEL_0), .IN1(IN1[3:2]), .SEL_1(SEL_1), .IN2(IN2[3:2]), .SEL_2(SEL_2),
    .IN3(IN3[3:2]), .SEL_3(SEL_3), .IN4(IN4[3:2]), .SEL_4(SEL_4), .IN5(IN5[3:2]), .SEL_5(SEL_5),
    .IN6(IN6[3:2]), .SEL_6(SEL_6), .IN7(IN7[3:2]), .SEL_7(SEL_7), .IN8(IN8[3:2]), .SEL_8(SEL_8),
    .IN9(IN9[3:2]), .SEL_9(SEL_9), .IN10(IN10[3:2]), .SEL_10(SEL_10), .IN11(IN11[3:2]), .SEL_11(SEL_11),
    .IN12(IN12[3:2]), .SEL_12(SEL_12), .IN13(IN13[3:2]), .SEL_13(SEL_13), .IN14(IN14[3:2]), .SEL_14(SEL_14),
    .IN15(IN15[3:2]), .SEL_15(SEL_15), .out_33(O[3:2]));
endmodule

module Onehotmux_16to1_8bit (
  input  [7:0] IN0,
  input  SEL_0,
  input  [7:0] IN1,
  input  SEL_1,
  input  [7:0] IN2,
  input  SEL_2,
  input  [7:0] IN3,
  input  SEL_3,
  input  [7:0] IN4,
  input  SEL_4,
  input  [7:0] IN5,
  input  SEL_5,
  input  [7:0] IN6,
  input  SEL_6,
  input  [7:0] IN7,
  input  SEL_7,
  input  [7:0] IN8,
  input  SEL_8,
  input  [7:0] IN9,
  input  SEL_9,
  input  [7:0] IN10,
  input  SEL_10,
  input  [7:0] IN11,
  input  SEL_11,
  input  [7:0] IN12,
  input  SEL_12,
  input  [7:0] IN13,
  input  SEL_13,
  input  [7:0] IN14,
  input  SEL_14,
  input  [7:0] IN15,
  input  SEL_15,
  output [7:0] O
);

  Onehotmux_16to1_4bit onehotmux_16to1_4bit_1 (
    .IN0(IN0[3:0]), .SEL_0(SEL_0), .IN1(IN1[3:0]), .SEL_1(SEL_1), .IN2(IN2[3:0]), .SEL_2(SEL_2),
    .IN3(IN3[3:0]), .SEL_3(SEL_3), .IN4(IN4[3:0]), .SEL_4(SEL_4), .IN5(IN5[3:0]), .SEL_5(SEL_5),
    .IN6(IN6[3:0]), .SEL_6(SEL_6), .IN7(IN7[3:0]), .SEL_7(SEL_7), .IN8(IN8[3:0]), .SEL_8(SEL_8),
    .IN9(IN9[3:0]), .SEL_9(SEL_9), .IN10(IN10[3:0]), .SEL_10(SEL_10), .IN11(IN11[3:0]), .SEL_11(SEL_11),
    .IN12(IN12[3:0]), .SEL_12(SEL_12), .IN13(IN13[3:0]), .SEL_13(SEL_13), .IN14(IN14[3:0]), .SEL_14(SEL_14),
    .IN15(IN15[3:0]), .SEL_15(SEL_15), .O(O[3:0]));
  Onehotmux_16to1_4bit onehotmux_16to1_4bit_2 (
    .IN0(IN0[7:4]), .SEL_0(SEL_0), .IN1(IN1[7:4]), .SEL_1(SEL_1), .IN2(IN2[7:4]), .SEL_2(SEL_2),
    .IN3(IN3[7:4]), .SEL_3(SEL_3), .IN4(IN4[7:4]), .SEL_4(SEL_4), .IN5(IN5[7:4]), .SEL_5(SEL_5),
    .IN6(IN6[7:4]), .SEL_6(SEL_6), .IN7(IN7[7:4]), .SEL_7(SEL_7), .IN8(IN8[7:4]), .SEL_8(SEL_8),
    .IN9(IN9[7:4]), .SEL_9(SEL_9), .IN10(IN10[7:4]), .SEL_10(SEL_10), .IN11(IN11[7:4]), .SEL_11(SEL_11),
    .IN12(IN12[7:4]), .SEL_12(SEL_12), .IN13(IN13[7:4]), .SEL_13(SEL_13), .IN14(IN14[7:4]), .SEL_14(SEL_14),
    .IN15(IN15[7:4]), .SEL_15(SEL_15), .O(O[7:4]));
endmodule

module MeomoryBank_16x8 (
  input  [7:0] IN_PUT,
  input  [3:0] Address,
  input  Write,
  output [7:0] O
);

  wire decoderdemux_4to16_1_d0, decoderdemux_4to16_1_d1, decoderdemux_4to16_1_d2, decoderdemux_4to16_1_d3,
       decoderdemux_4to16_1_d4, decoderdemux_4to16_1_d5, decoderdemux_4to16_1_d6, decoderdemux_4to16_1_d7,
       decoderdemux_4to16_1_d8, decoderdemux_4to16_1_d9, decoderdemux_4to16_1_d10, decoderdemux_4to16_1_d11,
       decoderdemux_4to16_1_d12, decoderdemux_4to16_1_d13, decoderdemux_4to16_1_d14,
       decoderdemux_4to16_1_d15, decoderdemux_4to16_1_y0, decoderdemux_4to16_1_y1, decoderdemux_4to16_1_y2,
       decoderdemux_4to16_1_y3, decoderdemux_4to16_1_y4, decoderdemux_4to16_1_y5, decoderdemux_4to16_1_y6,
       decoderdemux_4to16_1_y7, decoderdemux_4to16_1_y8, decoderdemux_4to16_1_y9, decoderdemux_4to16_1_y10,
       decoderdemux_4to16_1_y11, decoderdemux_4to16_1_y12, decoderdemux_4to16_1_y13,
       decoderdemux_4to16_1_y14, decoderdemux_4to16_1_y15;
  wire [7:0] WORD0_q, WORD1_q, WORD2_q, WORD3_q, WORD4_q, WORD5_q, WORD6_q, WORD7_q, WORD8_q, WORD9_q,
       WORD10_q, WORD11_q, WORD12_q, WORD13_q, WORD14_q, WORD15_q;

  DecoderDemux_4to16 decoderdemux_4to16_1 (
    .A0(Address[0]), .A1(Address[1]), .A2(Address[2]), .A3(Address[3]), .X(Write),
    .D0(decoderdemux_4to16_1_d0), .D1(decoderdemux_4to16_1_d1), .D2(decoderdemux_4to16_1_d2),
    .D3(decoderdemux_4to16_1_d3), .D4(decoderdemux_4to16_1_d4), .D5(decoderdemux_4to16_1_d5),
    .D6(decoderdemux_4to16_1_d6), .D7(decoderdemux_4to16_1_d7), .D8(decoderdemux_4to16_1_d8),
    .D9(decoderdemux_4to16_1_d9), .D10(decoderdemux_4to16_1_d10), .D11(decoderdemux_4to16_1_d11),
    .D12(decoderdemux_4to16_1_d12), .D13(decoderdemux_4to16_1_d13), .D14(decoderdemux_4to16_1_d14),
    .D15(decoderdemux_4to16_1_d15), .Y0(decoderdemux_4to16_1_y0), .Y1(decoderdemux_4to16_1_y1),
    .Y2(decoderdemux_4to16_1_y2), .Y3(decoderdemux_4to16_1_y3), .Y4(decoderdemux_4to16_1_y4),
    .Y5(decoderdemux_4to16_1_y5), .Y6(decoderdemux_4to16_1_y6), .Y7(decoderdemux_4to16_1_y7),
    .Y8(decoderdemux_4to16_1_y8), .Y9(decoderdemux_4to16_1_y9), .Y10(decoderdemux_4to16_1_y10),
    .Y11(decoderdemux_4to16_1_y11), .Y12(decoderdemux_4to16_1_y12), .Y13(decoderdemux_4to16_1_y13),
    .Y14(decoderdemux_4to16_1_y14), .Y15(decoderdemux_4to16_1_y15));
  // Probe on decoderdemux_4to16_1_y0
  // Probe on decoderdemux_4to16_1_d0
  // Probe on WORD0_q
  Register WORD0 (.D(IN_PUT), .en(decoderdemux_4to16_1_y0), .clk(1'b0), .Q(WORD0_q));  // open: clr
  Register WORD1 (.D(IN_PUT), .en(decoderdemux_4to16_1_y1), .clk(1'b0), .Q(WORD1_q));  // open: clr
  Register WORD2 (.D(IN_PUT), .en(decoderdemux_4to16_1_y2), .clk(1'b0), .Q(WORD2_q));  // open: clr
  Register WORD3 (.D(IN_PUT), .en(decoderdemux_4to16_1_y3), .clk(1'b0), .Q(WORD3_q));  // open: clr
  Register WORD4 (.D(IN_PUT), .en(decoderdemux_4to16_1_y4), .clk(1'b0), .Q(WORD4_q));  // open: clr
  Register WORD5 (.D(IN_PUT), .en(decoderdemux_4to16_1_y5), .clk(1'b0), .Q(WORD5_q));  // open: clr
  Register WORD6 (.D(IN_PUT), .en(decoderdemux_4to16_1_y6), .clk(1'b0), .Q(WORD6_q));  // open: clr
  Register WORD7 (.D(IN_PUT), .en(decoderdemux_4to16_1_y7), .clk(1'b0), .Q(WORD7_q));  // open: clr
  Register WORD8 (.D(IN_PUT), .en(decoderdemux_4to16_1_y8), .clk(1'b0), .Q(WORD8_q));  // open: clr
  Register WORD9 (.D(IN_PUT), .en(decoderdemux_4to16_1_y9), .clk(1'b0), .Q(WORD9_q));  // open: clr
  Register WORD10 (.D(IN_PUT), .en(decoderdemux_4to16_1_y10), .clk(1'b0), .Q(WORD10_q));  // open: clr
  Register WORD11 (.D(IN_PUT), .en(decoderdemux_4to16_1_y11), .clk(1'b0), .Q(WORD11_q));  // open: clr
  Register WORD12 (.D(IN_PUT), .en(decoderdemux_4to16_1_y12), .clk(1'b0), .Q(WORD12_q));  // open: clr
  Register WORD13 (.D(IN_PUT), .en(decoderdemux_4to16_1_y13), .clk(1'b0), .Q(WORD13_q));  // open: clr
  Register WORD14 (.D(IN_PUT), .en(decoderdemux_4to16_1_y14), .clk(1'b0), .Q(WORD14_q));  // open: clr
  Register WORD15 (.D(IN_PUT), .en(decoderdemux_4to16_1_y15), .clk(1'b0), .Q(WORD15_q));  // open: clr
  Onehotmux_16to1_8bit onehotmux_16to1_8bit_1 (
    .IN0(WORD0_q), .SEL_0(decoderdemux_4to16_1_d0), .IN1(WORD1_q), .SEL_1(decoderdemux_4to16_1_d1),
    .IN2(WORD2_q), .SEL_2(decoderdemux_4to16_1_d2), .IN3(WORD3_q), .SEL_3(decoderdemux_4to16_1_d3),
    .IN4(WORD4_q), .SEL_4(decoderdemux_4to16_1_d4), .IN5(WORD5_q), .SEL_5(decoderdemux_4to16_1_d5),
    .IN6(WORD6_q), .SEL_6(decoderdemux_4to16_1_d6), .IN7(WORD7_q), .SEL_7(decoderdemux_4to16_1_d7),
    .IN8(WORD8_q), .SEL_8(decoderdemux_4to16_1_d8), .IN9(WORD9_q), .SEL_9(decoderdemux_4to16_1_d9),
    .IN10(WORD10_q), .SEL_10(decoderdemux_4to16_1_d10), .IN11(WORD11_q), .SEL_11(decoderdemux_4to16_1_d11),
    .IN12(WORD12_q), .SEL_12(decoderdemux_4to16_1_d12), .IN13(WORD13_q), .SEL_13(decoderdemux_4to16_1_d13),
    .IN14(WORD14_q), .SEL_14(decoderdemux_4to16_1_d14), .IN15(WORD15_q), .SEL_15(decoderdemux_4to16_1_d15),
    .O(O));
endmodule

module MeomoryBank_16x8_v2 (
  input  [7:0] IN_PUT,
  input  [3:0] Address,
  input  Write,
  input  Clock,
  output [7:0] O
);

  wire decoderdemux_4to16_1_d0, decoderdemux_4to16_1_d1, decoderdemux_4to16_1_d2, decoderdemux_4to16_1_d3,
       decoderdemux_4to16_1_d4, decoderdemux_4to16_1_d5, decoderdemux_4to16_1_d6, decoderdemux_4to16_1_d7,
       decoderdemux_4to16_1_d8, decoderdemux_4to16_1_d9, decoderdemux_4to16_1_d10, decoderdemux_4to16_1_d11,
       decoderdemux_4to16_1_d12, decoderdemux_4to16_1_d13, decoderdemux_4to16_1_d14,
       decoderdemux_4to16_1_d15, decoderdemux_4to16_1_y0, decoderdemux_4to16_1_y1, decoderdemux_4to16_1_y2,
       decoderdemux_4to16_1_y3, decoderdemux_4to16_1_y4, decoderdemux_4to16_1_y5, decoderdemux_4to16_1_y6,
       decoderdemux_4to16_1_y7, decoderdemux_4to16_1_y8, decoderdemux_4to16_1_y9, decoderdemux_4to16_1_y10,
       decoderdemux_4to16_1_y11, decoderdemux_4to16_1_y12, decoderdemux_4to16_1_y13,
       decoderdemux_4to16_1_y14, decoderdemux_4to16_1_y15;
  wire [7:0] register_8bit_1_o, register_8bit_2_o, register_8bit_3_o, register_8bit_4_o, register_8bit_5_o,
       register_8bit_6_o, register_8bit_7_o, register_8bit_8_o, register_8bit_9_o, register_8bit_10_o,
       register_8bit_11_o, register_8bit_12_o, register_8bit_13_o, register_8bit_14_o, register_8bit_15_o,
       register_8bit_16_o;

  DecoderDemux_4to16 decoderdemux_4to16_1 (
    .A0(Address[0]), .A1(Address[1]), .A2(Address[2]), .A3(Address[3]), .X(Write),
    .D0(decoderdemux_4to16_1_d0), .D1(decoderdemux_4to16_1_d1), .D2(decoderdemux_4to16_1_d2),
    .D3(decoderdemux_4to16_1_d3), .D4(decoderdemux_4to16_1_d4), .D5(decoderdemux_4to16_1_d5),
    .D6(decoderdemux_4to16_1_d6), .D7(decoderdemux_4to16_1_d7), .D8(decoderdemux_4to16_1_d8),
    .D9(decoderdemux_4to16_1_d9), .D10(decoderdemux_4to16_1_d10), .D11(decoderdemux_4to16_1_d11),
    .D12(decoderdemux_4to16_1_d12), .D13(decoderdemux_4to16_1_d13), .D14(decoderdemux_4to16_1_d14),
    .D15(decoderdemux_4to16_1_d15), .Y0(decoderdemux_4to16_1_y0), .Y1(decoderdemux_4to16_1_y1),
    .Y2(decoderdemux_4to16_1_y2), .Y3(decoderdemux_4to16_1_y3), .Y4(decoderdemux_4to16_1_y4),
    .Y5(decoderdemux_4to16_1_y5), .Y6(decoderdemux_4to16_1_y6), .Y7(decoderdemux_4to16_1_y7),
    .Y8(decoderdemux_4to16_1_y8), .Y9(decoderdemux_4to16_1_y9), .Y10(decoderdemux_4to16_1_y10),
    .Y11(decoderdemux_4to16_1_y11), .Y12(decoderdemux_4to16_1_y12), .Y13(decoderdemux_4to16_1_y13),
    .Y14(decoderdemux_4to16_1_y14), .Y15(decoderdemux_4to16_1_y15));
  Register_8Bit register_8bit_1 (
    .IN_PUT(IN_PUT), .WRITE(decoderdemux_4to16_1_y0), .CLOCK(Clock), .O(register_8bit_1_o));
  Register_8Bit register_8bit_2 (
    .IN_PUT(IN_PUT), .WRITE(decoderdemux_4to16_1_y1), .CLOCK(Clock), .O(register_8bit_2_o));
  Register_8Bit register_8bit_3 (
    .IN_PUT(IN_PUT), .WRITE(decoderdemux_4to16_1_y2), .CLOCK(Clock), .O(register_8bit_3_o));
  Register_8Bit register_8bit_4 (
    .IN_PUT(IN_PUT), .WRITE(decoderdemux_4to16_1_y3), .CLOCK(Clock), .O(register_8bit_4_o));
  Register_8Bit register_8bit_5 (
    .IN_PUT(IN_PUT), .WRITE(decoderdemux_4to16_1_y4), .CLOCK(Clock), .O(register_8bit_5_o));
  Register_8Bit register_8bit_6 (
    .IN_PUT(IN_PUT), .WRITE(decoderdemux_4to16_1_y5), .CLOCK(Clock), .O(register_8bit_6_o));
  Register_8Bit register_8bit_7 (
    .IN_PUT(IN_PUT), .WRITE(decoderdemux_4to16_1_y6), .CLOCK(Clock), .O(register_8bit_7_o));
  Register_8Bit register_8bit_8 (
    .IN_PUT(IN_PUT), .WRITE(decoderdemux_4to16_1_y7), .CLOCK(Clock), .O(register_8bit_8_o));
  Register_8Bit register_8bit_9 (
    .IN_PUT(IN_PUT), .WRITE(decoderdemux_4to16_1_y8), .CLOCK(Clock), .O(register_8bit_9_o));
  Register_8Bit register_8bit_10 (
    .IN_PUT(IN_PUT), .WRITE(decoderdemux_4to16_1_y9), .CLOCK(Clock), .O(register_8bit_10_o));
  Register_8Bit register_8bit_11 (
    .IN_PUT(IN_PUT), .WRITE(decoderdemux_4to16_1_y10), .CLOCK(Clock), .O(register_8bit_11_o));
  Register_8Bit register_8bit_12 (
    .IN_PUT(IN_PUT), .WRITE(decoderdemux_4to16_1_y11), .CLOCK(Clock), .O(register_8bit_12_o));
  Register_8Bit register_8bit_13 (
    .IN_PUT(IN_PUT), .WRITE(decoderdemux_4to16_1_y12), .CLOCK(Clock), .O(register_8bit_13_o));
  Register_8Bit register_8bit_14 (
    .IN_PUT(IN_PUT), .WRITE(decoderdemux_4to16_1_y13), .CLOCK(Clock), .O(register_8bit_14_o));
  Register_8Bit register_8bit_15 (
    .IN_PUT(IN_PUT), .WRITE(decoderdemux_4to16_1_y14), .CLOCK(Clock), .O(register_8bit_15_o));
  Register_8Bit register_8bit_16 (
    .IN_PUT(IN_PUT), .WRITE(decoderdemux_4to16_1_y15), .CLOCK(Clock), .O(register_8bit_16_o));
  Onehotmux_16to1_8bit onehotmux_16to1_8bit_1 (
    .IN0(register_8bit_1_o), .SEL_0(decoderdemux_4to16_1_d0), .IN1(register_8bit_2_o),
    .SEL_1(decoderdemux_4to16_1_d1), .IN2(register_8bit_3_o), .SEL_2(decoderdemux_4to16_1_d2),
    .IN3(register_8bit_4_o), .SEL_3(decoderdemux_4to16_1_d3), .IN4(register_8bit_5_o),
    .SEL_4(decoderdemux_4to16_1_d4), .IN5(register_8bit_6_o), .SEL_5(decoderdemux_4to16_1_d5),
    .IN6(register_8bit_7_o), .SEL_6(decoderdemux_4to16_1_d6), .IN7(register_8bit_8_o),
    .SEL_7(decoderdemux_4to16_1_d7), .IN8(register_8bit_9_o), .SEL_8(decoderdemux_4to16_1_d8),
    .IN9(register_8bit_10_o), .SEL_9(decoderdemux_4to16_1_d9), .IN10(register_8bit_11_o),
    .SEL_10(decoderdemux_4to16_1_d10), .IN11(register_8bit_12_o), .SEL_11(decoderdemux_4to16_1_d11),
    .IN12(register_8bit_13_o), .SEL_12(decoderdemux_4to16_1_d12), .IN13(register_8bit_14_o),
    .SEL_13(decoderdemux_4to16_1_d13), .IN14(register_8bit_15_o), .SEL_14(decoderdemux_4to16_1_d14),
    .IN15(register_8bit_16_o), .SEL_15(decoderdemux_4to16_1_d15), .O(O));
endmodule

module Increment_4bit (
  input  [3:0] IN_PUT,
  output [3:0] OUT_PUT,
  output COUT
);

  bitadder4_v2 bitadder4_v2_1 (.A(IN_PUT), .B(4'b0001), .CIN(1'b0), .sout(OUT_PUT), .COUT(COUT));
endmodule

module Mux_2to1_4bit (
  input  [3:0] IN0,
  input  [3:0] IN1,
  input  SELECTION,
  output [3:0] OUT_PUT
);

  Multiplex_2to1 multiplex_2to1_1 (.A(IN0[0]), .B(IN1[0]), .SelectionLine(SELECTION), .O(OUT_PUT[0]));
  Multiplex_2to1 multiplex_2to1_2 (.A(IN0[1]), .B(IN1[1]), .SelectionLine(SELECTION), .O(OUT_PUT[1]));
  Multiplex_2to1 multiplex_2to1_3 (.A(IN0[2]), .B(IN1[2]), .SelectionLine(SELECTION), .O(OUT_PUT[2]));
  Multiplex_2to1 multiplex_2to1_4 (.A(IN0[3]), .B(IN1[3]), .SelectionLine(SELECTION), .O(OUT_PUT[3]));
endmodule

module PC_4BIT (
  input  [3:0] LOAD_IN,
  input  LOAD,
  input  WRITE,
  input  CLOCK,
  output [3:0] PC_OUT
);

  wire increment_4bit_1_cout;
  wire [3:0] increment_4bit_1_out_put, mux_2to1_4bit_1_out_put;

  Register_4Bit register_4bit_1 (.IN_PUT(mux_2to1_4bit_1_out_put), .WRITE(WRITE), .CLOCK(CLOCK), .out_4(PC_OUT));
  Increment_4bit increment_4bit_1 (.IN_PUT(PC_OUT), .OUT_PUT(increment_4bit_1_out_put), .COUT(increment_4bit_1_cout));
  // Probe on increment_4bit_1_cout
  Mux_2to1_4bit mux_2to1_4bit_1 (
    .IN0(increment_4bit_1_out_put), .IN1(LOAD_IN), .SELECTION(LOAD), .OUT_PUT(mux_2to1_4bit_1_out_put));
endmodule

module FetchExecuteClock (
  input  CLOCK,
  input  RESET,
  output FETCH,
  output EXECUTE,
  output FETCH_WRITE,
  output EXECUTE_WRITE
);

  wire and_1_out, not_1_out, not_2_out;

  not not_1 (not_1_out, RESET);
  and and_1 (and_1_out, FETCH, not_1_out);
  not not_2 (not_2_out, CLOCK);
  Memory_bit PHASE (.IN_PUT(and_1_out), .write(1'b1), .CLOCK(not_2_out), .OUT_PUT(EXECUTE));
  not not_3 (FETCH, EXECUTE);
  and and_2 (FETCH_WRITE, FETCH, CLOCK);
  and and_3 (EXECUTE_WRITE, EXECUTE, CLOCK);
endmodule

module IR_Register (
  input  [7:0] INSTRUCTION_IN,
  input  IR_WRITE,
  input  CLOCK,
  output [7:0] IR_OUT
);

  Register_8Bit register_8bit_1 (.IN_PUT(INSTRUCTION_IN), .WRITE(IR_WRITE), .CLOCK(CLOCK), .O(IR_OUT));
endmodule

module R_Register (
  input  [7:0] R_IN,
  input  R_WRITE,
  input  CLOCK,
  output [7:0] R_OUT
);

  Register_8Bit register_8bit_1 (.IN_PUT(R_IN), .WRITE(R_WRITE), .CLOCK(CLOCK), .O(R_OUT));
endmodule

module Address_Mux (
  input  [3:0] PC_IN,
  input  [3:0] IR_ADDR_IN,
  input  EXECUTE,
  output [3:0] ADDRESS_OUT
);

  Mux_2to1_4bit mux_2to1_4bit_1 (.IN0(PC_IN), .IN1(IR_ADDR_IN), .SELECTION(EXECUTE), .OUT_PUT(ADDRESS_OUT));
endmodule

module OneHotMux_3to1_1BIT (
  input  IN0,
  input  SEL_0,
  input  IN1,
  input  SEL_1,
  input  IN2,
  input  SEL_2,
  output O
);

  wire and_1_out, and_2_out, and_3_out, or_1_out;

  and and_1 (and_1_out, IN0, SEL_0);
  and and_2 (and_2_out, IN1, SEL_1);
  and and_3 (and_3_out, IN2, SEL_2);
  or or_1 (or_1_out, and_1_out, and_2_out);
  or or_2 (O, or_1_out, and_3_out);
endmodule

module OneHotMux_3to1_2bit (
  input  [1:0] IN0,
  input  [1:0] IN1,
  input  [1:0] IN2,
  input  SEL_0,
  input  SEL_1,
  input  SEL_2,
  output [1:0] O
);

  OneHotMux_3to1_1BIT onehotmux_3to1_1bit_1 (
    .IN0(IN0[0]), .SEL_0(SEL_0), .IN1(IN1[0]), .SEL_1(SEL_1), .IN2(IN2[0]), .SEL_2(SEL_2), .O(O[0]));
  OneHotMux_3to1_1BIT onehotmux_3to1_1bit_2 (
    .IN0(IN0[1]), .SEL_0(SEL_0), .IN1(IN1[1]), .SEL_1(SEL_1), .IN2(IN2[1]), .SEL_2(SEL_2), .O(O[1]));
endmodule

module OneHotMux_3to1_4bit (
  input  [3:0] IN0,
  input  [3:0] IN1,
  input  [3:0] IN2,
  input  SEL_0,
  input  SEL_1,
  input  SEL_2,
  output [3:0] O
);

  OneHotMux_3to1_2bit onehotmux_3to1_2bit_1 (
    .IN0(IN0[1:0]), .IN1(IN1[1:0]), .IN2(IN2[1:0]), .SEL_0(SEL_0), .SEL_1(SEL_1), .SEL_2(SEL_2), .O(O[1:0]));
  OneHotMux_3to1_2bit onehotmux_3to1_2bit_2 (
    .IN0(IN0[3:2]), .IN1(IN1[3:2]), .IN2(IN2[3:2]), .SEL_0(SEL_0), .SEL_1(SEL_1), .SEL_2(SEL_2), .O(O[3:2]));
endmodule

module OneHotMux_3to1_8bit (
  input  [7:0] IN0,
  input  [7:0] IN1,
  input  [7:0] IN2,
  input  SEL_0,
  input  SEL_1,
  input  SEL_2,
  output [7:0] O
);

  OneHotMux_3to1_4bit onehotmux_3to1_4bit_1 (
    .IN0(IN0[3:0]), .IN1(IN1[3:0]), .IN2(IN2[3:0]), .SEL_0(SEL_0), .SEL_1(SEL_1), .SEL_2(SEL_2), .O(O[3:0]));
  OneHotMux_3to1_4bit onehotmux_3to1_4bit_2 (
    .IN0(IN0[7:4]), .IN1(IN1[7:4]), .IN2(IN2[7:4]), .SEL_0(SEL_0), .SEL_1(SEL_1), .SEL_2(SEL_2), .O(O[7:4]));
endmodule

module OneHotMux_3to1_16bit (
  input  [15:0] IN0,
  input  [15:0] IN1,
  input  [15:0] IN2,
  input  SEL_0,
  input  SEL_1,
  input  SEL_2,
  output [15:0] O
);

  OneHotMux_3to1_8bit onehotmux_3to1_8bit_1 (
    .IN0(IN0[7:0]), .IN1(IN1[7:0]), .IN2(IN2[7:0]), .SEL_0(SEL_0), .SEL_1(SEL_1), .SEL_2(SEL_2), .O(O[7:0]));
  OneHotMux_3to1_8bit onehotmux_3to1_8bit_2 (
    .IN0(IN0[15:8]), .IN1(IN1[15:8]), .IN2(IN2[15:8]), .SEL_0(SEL_0), .SEL_1(SEL_1), .SEL_2(SEL_2),
    .O(O[15:8]));
endmodule

module R_Mux (
  input  [7:0] ALU_IN,
  input  SEL_ALU,
  input  [7:0] MEMORY_IN,
  input  SEL_MEOMORY,
  input  [7:0] IR_VALUE_IN,
  input  SEL_IR,
  output [7:0] R_MUX_OUT
);

  OneHotMux_3to1_8bit onehotmux_3to1_8bit_1 (
    .IN0(ALU_IN), .IN1(MEMORY_IN), .IN2(IR_VALUE_IN), .SEL_0(SEL_ALU), .SEL_1(SEL_MEOMORY), .SEL_2(SEL_IR),
    .O(R_MUX_OUT));
endmodule

module Zero_check_8bit (
  input  [7:0] R_in,
  output R_Zero
);

  wire or_1_out, or_2_out, or_3_out, or_4_out, or_5_out, or_6_out, or_7_out;

  or or_1 (or_1_out, R_in[0], R_in[1]);
  or or_2 (or_2_out, or_1_out, R_in[2]);
  or or_3 (or_3_out, or_2_out, R_in[3]);
  or or_4 (or_4_out, or_3_out, R_in[4]);
  or or_5 (or_5_out, or_4_out, R_in[5]);
  or or_6 (or_6_out, or_5_out, R_in[6]);
  or or_7 (or_7_out, or_6_out, R_in[7]);
  not not_1 (R_Zero, or_7_out);
endmodule

module OR_3Input (
  input  A,
  input  B,
  input  C,
  output O
);

  wire or_1_out;

  or or_1 (or_1_out, A, B);
  or or_2 (O, or_1_out, C);
endmodule

module OR_5INPUT (
  input  A,
  input  B,
  input  C,
  input  D,
  input  E,
  output O
);

  wire or_1_out, or_2_out, or_3_out;

  or or_1 (or_1_out, A, B);
  or or_2 (or_2_out, or_1_out, C);
  or or_3 (or_3_out, or_2_out, D);
  or or_4 (O, or_3_out, E);
endmodule

module Control_Unit_TOY8 (
  input  [3:0] OPCODE,
  input  EXECUTE,
  input  FETCH,
  input  EXECUTE_WRITE,
  input  FETCH_WRITE,
  input  R_ZERO,
  output HALT,
  output ALU_ADD,
  output ALU_AND,
  output ALU_XOR,
  output R_MUX_ALU,
  output R_MUX_MEMORY,
  output R_MUX_IR,
  output R_WRITE,
  output MEMORY_WRITE,
  output IR_WRITE,
  output PC_LOAD,
  output PC_WRITE
);

  wire decoder_4to16_1_d0, decoder_4to16_1_d2, decoder_4to16_1_d4, decoder_4to16_1_d6, decoder_4to16_1_d8,
       decoder_4to16_1_d10, decoder_4to16_1_d12, decoder_4to16_1_d14, not_1_out, or_1_out, or_2_out;

  Decoder_4to16 decoder_4to16_1 (
    .A0(OPCODE[0]), .A1(OPCODE[1]), .A2(OPCODE[2]), .A3(OPCODE[3]), .D0(decoder_4to16_1_d0),
    .D2(decoder_4to16_1_d2), .D4(decoder_4to16_1_d4), .D6(decoder_4to16_1_d6), .D8(decoder_4to16_1_d8),
    .D10(decoder_4to16_1_d10), .D12(decoder_4to16_1_d12), .D14(decoder_4to16_1_d14));  // open: D1, D3, D5, D7, D9, D11, D13, D15
  not not_1 (not_1_out, decoder_4to16_1_d0);
  and and_1 (HALT, decoder_4to16_1_d0, EXECUTE);
  and and_2 (ALU_ADD, decoder_4to16_1_d2, EXECUTE);
  and and_3 (ALU_AND, decoder_4to16_1_d4, EXECUTE);
  and and_4 (ALU_XOR, decoder_4to16_1_d6, EXECUTE);
  or or_1 (or_1_out, decoder_4to16_1_d2, decoder_4to16_1_d4, decoder_4to16_1_d6);
  and and_5 (R_MUX_MEMORY, EXECUTE, decoder_4to16_1_d10);
  and and_6 (R_MUX_IR, decoder_4to16_1_d8, EXECUTE);
  or or_2 (or_2_out, decoder_4to16_1_d2, decoder_4to16_1_d4, decoder_4to16_1_d6, decoder_4to16_1_d8, decoder_4to16_1_d10);
  and and_7 (MEMORY_WRITE, decoder_4to16_1_d12, EXECUTE);
  and and_8 (PC_LOAD, decoder_4to16_1_d14, R_ZERO, EXECUTE);
  and and_9 (PC_WRITE, not_1_out, EXECUTE);
  and and_10 (R_MUX_ALU, or_1_out, EXECUTE);
  and and_11 (R_WRITE, or_2_out, EXECUTE);

  assign IR_WRITE = FETCH;
endmodule

module Main_CPU (
  input  GLOBAL_CLOCK,
  input  RESET,
  output FETCH,
  output EXECUTE,
  output HALT,
  output [3:0] ADDRESS_OUT,
  output [7:0] MEM_OUT,
  output [3:0] PC_OUT,
  output [7:0] IR_OUT,
  output [7:0] R_OUT
);

  wire alu_8bit_v2_1_cout, control_unit_toy8_1_alu_add, control_unit_toy8_1_alu_and,
       control_unit_toy8_1_alu_xor, control_unit_toy8_1_ir_write, control_unit_toy8_1_memory_write,
       control_unit_toy8_1_pc_load, control_unit_toy8_1_pc_write, control_unit_toy8_1_r_mux_alu,
       control_unit_toy8_1_r_mux_ir, control_unit_toy8_1_r_mux_memory, control_unit_toy8_1_r_write,
       fetchexecuteclock_1_execute_write, fetchexecuteclock_1_fetch_write, zero_check_8bit_1_r_zero;
  wire [7:0] alu_8bit_v2_1_alu_out, r_mux_1_r_mux_out;

  FetchExecuteClock fetchexecuteclock_1 (
    .CLOCK(GLOBAL_CLOCK), .RESET(RESET), .FETCH(FETCH), .EXECUTE(EXECUTE),
    .FETCH_WRITE(fetchexecuteclock_1_fetch_write), .EXECUTE_WRITE(fetchexecuteclock_1_execute_write));
  PC_4BIT pc_4bit_1 (
    .LOAD_IN(IR_OUT[3:0]), .LOAD(control_unit_toy8_1_pc_load), .WRITE(control_unit_toy8_1_pc_write),
    .CLOCK(GLOBAL_CLOCK), .PC_OUT(PC_OUT));
  R_Register r_register_1 (
    .R_IN(r_mux_1_r_mux_out), .R_WRITE(control_unit_toy8_1_r_write), .CLOCK(GLOBAL_CLOCK), .R_OUT(R_OUT));
  IR_Register ir_register_1 (
    .INSTRUCTION_IN(MEM_OUT), .IR_WRITE(control_unit_toy8_1_ir_write), .CLOCK(GLOBAL_CLOCK), .IR_OUT(IR_OUT));
  Zero_check_8bit zero_check_8bit_1 (.R_in(R_OUT), .R_Zero(zero_check_8bit_1_r_zero));
  // Probe on R_OUT
  // Probe on PC_OUT
  R_Mux r_mux_1 (
    .ALU_IN(alu_8bit_v2_1_alu_out), .SEL_ALU(control_unit_toy8_1_r_mux_alu), .MEMORY_IN(MEM_OUT),
    .SEL_MEOMORY(control_unit_toy8_1_r_mux_memory), .IR_VALUE_IN({4'b0000, IR_OUT[3:0]}),
    .SEL_IR(control_unit_toy8_1_r_mux_ir), .R_MUX_OUT(r_mux_1_r_mux_out));
  Control_Unit_TOY8 control_unit_toy8_1 (
    .OPCODE(IR_OUT[7:4]), .EXECUTE(EXECUTE), .FETCH(FETCH),
    .EXECUTE_WRITE(fetchexecuteclock_1_execute_write), .FETCH_WRITE(fetchexecuteclock_1_fetch_write),
    .R_ZERO(zero_check_8bit_1_r_zero), .HALT(HALT), .ALU_ADD(control_unit_toy8_1_alu_add),
    .ALU_AND(control_unit_toy8_1_alu_and), .ALU_XOR(control_unit_toy8_1_alu_xor),
    .R_MUX_ALU(control_unit_toy8_1_r_mux_alu), .R_MUX_MEMORY(control_unit_toy8_1_r_mux_memory),
    .R_MUX_IR(control_unit_toy8_1_r_mux_ir), .R_WRITE(control_unit_toy8_1_r_write),
    .MEMORY_WRITE(control_unit_toy8_1_memory_write), .IR_WRITE(control_unit_toy8_1_ir_write),
    .PC_LOAD(control_unit_toy8_1_pc_load), .PC_WRITE(control_unit_toy8_1_pc_write));
  Address_Mux address_mux_1 (.PC_IN(PC_OUT), .IR_ADDR_IN(IR_OUT[3:0]), .EXECUTE(EXECUTE), .ADDRESS_OUT(ADDRESS_OUT));
  ALU_8BIT_V2 alu_8bit_v2_1 (
    .A(R_OUT), .B(MEM_OUT), .SEL_ADD(control_unit_toy8_1_alu_add), .SEL_SUB(1'b0),
    .SEL_AND(control_unit_toy8_1_alu_and), .SEL_XOR(control_unit_toy8_1_alu_xor), .SEL_LShift(1'b0),
    .SEL_RShift(1'b0), .ALU_OUT(alu_8bit_v2_1_alu_out), .COUT(alu_8bit_v2_1_cout));
  // Probe on ADDRESS_OUT
  // Probe on alu_8bit_v2_1_cout
  // Probe on HALT
  RAM #(.addrWidth(4), .asyncread("true")) ram_1 (
    .addr(ADDRESS_OUT), .we(control_unit_toy8_1_memory_write), .oe(1'b1), .clk(GLOBAL_CLOCK), .din(R_OUT),
    .dout(MEM_OUT));
endmodule

module ram_testy (
  input  [3:0] in_1,
  input  in_2,
  input  in_3,
  input  [7:0] in_4,
  output [7:0] out_5
);

  RAM #(.addrWidth(4)) ram_1 (.addr(in_1), .we(in_2), .oe(1'b1), .clk(in_3), .din(in_4), .dout(out_5));
endmodule

module adder_16bit (
  input  [15:0] A,
  input  CIN,
  input  [15:0] B,
  output [15:0] O,
  output COUT
);

  wire bitadder8_v2_1_cout;

  bitadder8_v2 bitadder8_v2_1 (.A(A[7:0]), .B(B[7:0]), .Cin(CIN), .Sout(O[7:0]), .Cout(bitadder8_v2_1_cout));
  bitadder8_v2 bitadder8_v2_2 (.A(A[15:8]), .B(B[15:8]), .Cin(bitadder8_v2_1_cout), .Sout(O[15:8]), .Cout(COUT));
endmodule

module subtractor_16bit (
  input  [15:0] A,
  input  [15:0] B,
  output [15:0] O,
  output COUT
);

  wire [15:0] not_1_out;

  assign not_1_out = ~B;  // NOT_Gate not_1, 16 bits wide
  adder_16bit adder_16bit_1 (.A(A), .CIN(1'b1), .B(not_1_out), .O(O), .COUT(COUT));
endmodule

module NOT_16BIT (
  input  [15:0] A,
  output [15:0] O
);

  bit8NOT bit8not_1 (.A(A[7:0]), .B(O[7:0]));
  bit8NOT bit8not_2 (.A(A[15:8]), .B(O[15:8]));
endmodule

module AND_16BIT (
  input  [15:0] A,
  input  [15:0] B,
  output [15:0] O
);

  EightBitAND eightbitand_1 (.A(A[7:0]), .B(B[7:0]), .O(O[7:0]));
  EightBitAND eightbitand_2 (.A(A[15:8]), .B(B[15:8]), .O(O[15:8]));
endmodule

module XOR_16BIT (
  input  [15:0] A,
  input  [15:0] B,
  output [15:0] O
);

  EightBitXOR eightbitxor_1 (.A(A[7:0]), .B(B[7:0]), .O(O[7:0]));
  EightBitXOR eightbitxor_2 (.A(A[15:8]), .B(B[15:8]), .O(O[15:8]));
endmodule

module pass_B (
  input  [15:0] B,
  output [15:0] O
);


  assign O = B;
endmodule

module hotmux_7to1_1bit (
  input  IN0,
  input  SEL_0,
  input  IN1,
  input  SEL_1,
  input  IN2,
  input  SEL_2,
  input  IN3,
  input  SEL_3,
  input  IN4,
  input  SEL_4,
  input  IN5,
  input  SEL_5,
  input  IN6,
  input  SEL_6,
  output O
);

  wire and_1_out, and_2_out, and_3_out, and_4_out, and_5_out, and_6_out, and_7_out, or_1_out, or_2_out,
       or_3_out, or_4_out, or_5_out;

  and and_1 (and_1_out, IN0, SEL_0);
  and and_2 (and_2_out, IN1, SEL_1);
  and and_3 (and_3_out, IN2, SEL_2);
  and and_4 (and_4_out, IN3, SEL_3);
  and and_5 (and_5_out, IN4, SEL_4);
  and and_6 (and_6_out, IN5, SEL_5);
  and and_7 (and_7_out, IN6, SEL_6);
  or or_1 (or_1_out, and_1_out, and_2_out);
  or or_2 (or_2_out, or_1_out, and_3_out);
  or or_3 (or_3_out, or_2_out, and_4_out);
  or or_4 (or_4_out, or_3_out, and_5_out);
  or or_5 (or_5_out, or_4_out, and_6_out);
  or or_6 (O, or_5_out, and_7_out);
endmodule

module hotmux_7to1_2bit (
  input  [1:0] IN0,
  input  SEL_0,
  input  [1:0] IN1,
  input  SEL_1,
  input  [1:0] IN2,
  input  SEL_2,
  input  [1:0] IN3,
  input  SEL_3,
  input  [1:0] IN4,
  input  SEL_4,
  input  [1:0] IN5,
  input  SEL_5,
  input  [1:0] IN6,
  input  SEL_6,
  output [1:0] O
);

  hotmux_7to1_1bit hotmux_7to1_1bit_1 (
    .IN0(IN0[0]), .SEL_0(SEL_0), .IN1(IN1[0]), .SEL_1(SEL_1), .IN2(IN2[0]), .SEL_2(SEL_2), .IN3(IN3[0]),
    .SEL_3(SEL_3), .IN4(IN4[0]), .SEL_4(SEL_4), .IN5(IN5[0]), .SEL_5(SEL_5), .IN6(IN6[0]), .SEL_6(SEL_6),
    .O(O[0]));
  hotmux_7to1_1bit hotmux_7to1_1bit_2 (
    .IN0(IN0[1]), .SEL_0(SEL_0), .IN1(IN1[1]), .SEL_1(SEL_1), .IN2(IN2[1]), .SEL_2(SEL_2), .IN3(IN3[1]),
    .SEL_3(SEL_3), .IN4(IN4[1]), .SEL_4(SEL_4), .IN5(IN5[1]), .SEL_5(SEL_5), .IN6(IN6[1]), .SEL_6(SEL_6),
    .O(O[1]));
endmodule

module HOTMUX_7TO1_4BIT (
  input  [3:0] IN0,
  input  SEL_0,
  input  [3:0] IN1,
  input  SEL_1,
  input  [3:0] IN2,
  input  SEL_2,
  input  [3:0] IN3,
  input  SEL_3,
  input  [3:0] IN4,
  input  SEL_4,
  input  [3:0] IN5,
  input  SEL_5,
  input  [3:0] IN6,
  input  SEL_6,
  output [3:0] O
);

  hotmux_7to1_2bit hotmux_7to1_2bit_1 (
    .IN0(IN0[1:0]), .SEL_0(SEL_0), .IN1(IN1[1:0]), .SEL_1(SEL_1), .IN2(IN2[1:0]), .SEL_2(SEL_2),
    .IN3(IN3[1:0]), .SEL_3(SEL_3), .IN4(IN4[1:0]), .SEL_4(SEL_4), .IN5(IN5[1:0]), .SEL_5(SEL_5),
    .IN6(IN6[1:0]), .SEL_6(SEL_6), .O(O[1:0]));
  hotmux_7to1_2bit hotmux_7to1_2bit_2 (
    .IN0(IN0[3:2]), .SEL_0(SEL_0), .IN1(IN1[3:2]), .SEL_1(SEL_1), .IN2(IN2[3:2]), .SEL_2(SEL_2),
    .IN3(IN3[3:2]), .SEL_3(SEL_3), .IN4(IN4[3:2]), .SEL_4(SEL_4), .IN5(IN5[3:2]), .SEL_5(SEL_5),
    .IN6(IN6[3:2]), .SEL_6(SEL_6), .O(O[3:2]));
endmodule

module HOTMUX_7TO1_8BIT (
  input  [7:0] IN0,
  input  SEL_0,
  input  [7:0] IN1,
  input  SEL_1,
  input  [7:0] IN2,
  input  SEL_2,
  input  [7:0] IN3,
  input  SEL_3,
  input  [7:0] IN4,
  input  SEL_4,
  input  [7:0] IN5,
  input  SEL_5,
  input  [7:0] IN6,
  input  SEL_6,
  output [7:0] O
);

  HOTMUX_7TO1_4BIT hotmux_7to1_4bit_1 (
    .IN0(IN0[3:0]), .SEL_0(SEL_0), .IN1(IN1[3:0]), .SEL_1(SEL_1), .IN2(IN2[3:0]), .SEL_2(SEL_2),
    .IN3(IN3[3:0]), .SEL_3(SEL_3), .IN4(IN4[3:0]), .SEL_4(SEL_4), .IN5(IN5[3:0]), .SEL_5(SEL_5),
    .IN6(IN6[3:0]), .SEL_6(SEL_6), .O(O[3:0]));
  HOTMUX_7TO1_4BIT hotmux_7to1_4bit_2 (
    .IN0(IN0[7:4]), .SEL_0(SEL_0), .IN1(IN1[7:4]), .SEL_1(SEL_1), .IN2(IN2[7:4]), .SEL_2(SEL_2),
    .IN3(IN3[7:4]), .SEL_3(SEL_3), .IN4(IN4[7:4]), .SEL_4(SEL_4), .IN5(IN5[7:4]), .SEL_5(SEL_5),
    .IN6(IN6[7:4]), .SEL_6(SEL_6), .O(O[7:4]));
endmodule

module HOTMUX_7TO1_16BIT (
  input  [15:0] IN0,
  input  SEL_0,
  input  [15:0] IN1,
  input  SEL_1,
  input  [15:0] IN2,
  input  SEL_2,
  input  [15:0] IN3,
  input  SEL_3,
  input  [15:0] IN4,
  input  SEL_4,
  input  [15:0] IN5,
  input  SEL_5,
  input  [15:0] IN6,
  input  SEL_6,
  output [15:0] O
);

  HOTMUX_7TO1_8BIT hotmux_7to1_8bit_1 (
    .IN0(IN0[7:0]), .SEL_0(SEL_0), .IN1(IN1[7:0]), .SEL_1(SEL_1), .IN2(IN2[7:0]), .SEL_2(SEL_2),
    .IN3(IN3[7:0]), .SEL_3(SEL_3), .IN4(IN4[7:0]), .SEL_4(SEL_4), .IN5(IN5[7:0]), .SEL_5(SEL_5),
    .IN6(IN6[7:0]), .SEL_6(SEL_6), .O(O[7:0]));
  HOTMUX_7TO1_8BIT hotmux_7to1_8bit_2 (
    .IN0(IN0[15:8]), .SEL_0(SEL_0), .IN1(IN1[15:8]), .SEL_1(SEL_1), .IN2(IN2[15:8]), .SEL_2(SEL_2),
    .IN3(IN3[15:8]), .SEL_3(SEL_3), .IN4(IN4[15:8]), .SEL_4(SEL_4), .IN5(IN5[15:8]), .SEL_5(SEL_5),
    .IN6(IN6[15:8]), .SEL_6(SEL_6), .O(O[15:8]));
endmodule

module ALU_16BIT (
  input  [15:0] A,
  input  [15:0] B,
  input  SEL_ADD,
  input  SEL_SUB,
  input  SEL_AND,
  input  SEL_XOR,
  input  SEL_SHL,
  input  SEL_SHR,
  input  SEL_PASS_B,
  output [15:0] O,
  output ZERO,
  output COUT,
  output POSITIVE
);

  wire adder_16bit_1_cout, and_1_out, and_2_out, not_1_out, not_3_out, or_2_out, subtractor_16bit_1_cout;
  wire [15:0] adder_16bit_1_o, and_16bit_1_o, pass_b_1_o, shl_16bit_var_1_o, shr_16bit_var_1_o,
       subtractor_16bit_1_o, xor_16bit_1_o;

  adder_16bit adder_16bit_1 (.A(A), .B(B), .O(adder_16bit_1_o), .COUT(adder_16bit_1_cout));  // open: CIN
  subtractor_16bit subtractor_16bit_1 (.A(A), .B(B), .O(subtractor_16bit_1_o), .COUT(subtractor_16bit_1_cout));
  AND_16BIT and_16bit_1 (.A(A), .B(B), .O(and_16bit_1_o));
  XOR_16BIT xor_16bit_1 (.A(A), .B(B), .O(xor_16bit_1_o));
  SHL_16BIT_VAR shl_16bit_var_1 (.A(A), .B(B), .O(shl_16bit_var_1_o));
  SHR_16BIT_VAR shr_16bit_var_1 (.A(A), .B(B), .O(shr_16bit_var_1_o));
  pass_B pass_b_1 (.B(B), .O(pass_b_1_o));
  and and_1 (and_1_out, adder_16bit_1_cout, SEL_ADD);
  and and_2 (and_2_out, subtractor_16bit_1_cout, SEL_SUB);
  HOTMUX_7TO1_16BIT hotmux_7to1_16bit_1 (
    .IN0(adder_16bit_1_o), .SEL_0(SEL_ADD), .IN1(subtractor_16bit_1_o), .SEL_1(SEL_SUB), .IN2(and_16bit_1_o),
    .SEL_2(SEL_AND), .IN3(xor_16bit_1_o), .SEL_3(SEL_XOR), .IN4(shl_16bit_var_1_o), .SEL_4(SEL_SHL),
    .IN5(shr_16bit_var_1_o), .SEL_5(SEL_SHR), .IN6(pass_b_1_o), .SEL_6(SEL_PASS_B), .O(O));
  or or_1 (COUT, and_1_out, and_2_out);
  not not_1 (not_1_out, O[15]);
  or or_2 (or_2_out, O[0], O[1], O[2], O[3], O[4], O[5], O[6], O[7], O[8], O[9], O[10], O[11], O[12], O[13], O[14], O[15]);
  not not_2 (ZERO, or_2_out);
  not not_3 (not_3_out, ZERO);
  and and_3 (POSITIVE, not_1_out, not_3_out);
endmodule

module Increment_8bit (
  input  [7:0] A,
  output [7:0] O,
  output COUT
);

  bitadder8_v2 bitadder8_v2_1 (.A(A), .B(8'h1), .Cin(1'b0), .Sout(O), .Cout(COUT));
endmodule

module hotmux_2to1_1bit (
  input  IN0,
  input  IN1,
  input  SEL,
  output O
);

  wire and_1_out, and_2_out, not_1_out;

  not not_1 (not_1_out, SEL);
  and and_1 (and_1_out, IN0, not_1_out);
  and and_2 (and_2_out, IN1, SEL);
  or or_1 (O, and_1_out, and_2_out);
endmodule

module hotmuux_2to1_2bit (
  input  [1:0] A,
  input  [1:0] B,
  input  SEL,
  output [1:0] O
);

  hotmux_2to1_1bit hotmux_2to1_1bit_1 (.IN0(A[0]), .IN1(B[0]), .SEL(SEL), .O(O[0]));
  hotmux_2to1_1bit hotmux_2to1_1bit_2 (.IN0(A[1]), .IN1(B[1]), .SEL(SEL), .O(O[1]));
endmodule

module HOTMUX_2TO1_4BIT (
  input  [3:0] A,
  input  [3:0] B,
  input  SEL,
  output [3:0] O
);

  hotmuux_2to1_2bit hotmuux_2to1_2bit_1 (.A(A[1:0]), .B(B[1:0]), .SEL(SEL), .O(O[1:0]));
  hotmuux_2to1_2bit hotmuux_2to1_2bit_2 (.A(A[3:2]), .B(B[3:2]), .SEL(SEL), .O(O[3:2]));
endmodule

module HOTMUX_2TO1_8BIT (
  input  [7:0] A,
  input  [7:0] B,
  input  SEL,
  output [7:0] O
);

  HOTMUX_2TO1_4BIT hotmux_2to1_4bit_1 (.A(A[3:0]), .B(B[3:0]), .SEL(SEL), .O(O[3:0]));
  HOTMUX_2TO1_4BIT hotmux_2to1_4bit_2 (.A(A[7:4]), .B(B[7:4]), .SEL(SEL), .O(O[7:4]));
endmodule

module hotmux_2to1_16bit (
  input  [15:0] A,
  input  [15:0] B,
  input  SEL,
  output [15:0] O
);

  HOTMUX_2TO1_8BIT hotmux_2to1_8bit_1 (.A(A[7:0]), .B(B[7:0]), .SEL(SEL), .O(O[7:0]));
  HOTMUX_2TO1_8BIT hotmux_2to1_8bit_2 (.A(A[15:8]), .B(B[15:8]), .SEL(SEL), .O(O[15:8]));
endmodule

module PC_8BIT (
  input  [7:0] Load_IN,
  input  Load,
  input  Write,
  input  Clock,
  output [7:0] PC_OUT,
  output cout
);

  wire [7:0] hotmux_2to1_8bit_1_o, increment_8bit_1_o;

  Register_8Bit register_8bit_1 (.IN_PUT(hotmux_2to1_8bit_1_o), .WRITE(Write), .CLOCK(Clock), .O(PC_OUT));
  Increment_8bit increment_8bit_1 (.A(PC_OUT), .O(increment_8bit_1_o), .COUT(cout));
  HOTMUX_2TO1_8BIT hotmux_2to1_8bit_1 (.A(increment_8bit_1_o), .B(Load_IN), .SEL(Load), .O(hotmux_2to1_8bit_1_o));
endmodule

module Rejister_16bit (
  input  [15:0] Data,
  input  Write,
  input  Clock,
  output [15:0] O
);

  Register_8Bit register_8bit_1 (.IN_PUT(Data[7:0]), .WRITE(Write), .CLOCK(Clock), .O(O[7:0]));
  Register_8Bit register_8bit_2 (.IN_PUT(Data[15:8]), .WRITE(Write), .CLOCK(Clock), .O(O[15:8]));
endmodule

module IR_Register_16bit (
  input  [15:0] Instruction_In,
  input  IR_Write,
  input  Clock,
  output [15:0] IR_OUT
);

  Rejister_16bit rejister_16bit_1 (.Data(Instruction_In), .Write(IR_Write), .Clock(Clock), .O(IR_OUT));
endmodule

module RAM_256x16 (
  input  [7:0] Address,
  input  MEM_Write,
  input  [15:0] DATA_IN,
  input  Clock,
  output [15:0] Mem_Out
);

  RAM #(.asyncread("true"), .dataWidth(16)) ram_1 (
    .addr(Address), .we(MEM_Write), .oe(1'b1), .clk(Clock), .din(DATA_IN), .dout(Mem_Out));
endmodule

module Decoder_2to4 (
  input  [1:0] AB,
  output D0,
  output D1,
  output D2,
  output D3
);

  wire not_1_out, not_2_out, not_3_out, not_4_out;

  not not_1 (not_1_out, AB[0]);
  not not_2 (not_2_out, AB[1]);
  not not_3 (not_3_out, AB[1]);
  not not_4 (not_4_out, AB[0]);
  and and_1 (D0, not_1_out, not_2_out);
  and and_2 (D1, AB[0], not_3_out);
  and and_3 (D2, not_4_out, AB[1]);
  and and_4 (D3, AB[0], AB[1]);
endmodule

module Counter_2bit_ff (
  input  Clock,
  input  Reset,
  output Q0,
  output [1:0] Count,
  output Q1
);

  wire not_1_out, xor_1_out;

  D_Flip_Flop d_ff_1 (.D(not_1_out), .clk(Clock), .Q(Count[0]), .reset(Reset));  // open: Qn, preset
  D_Flip_Flop d_ff_2 (.D(xor_1_out), .clk(Clock), .Q(Count[1]), .reset(Reset));  // open: Qn, preset
  not not_1 (not_1_out, Count[0]);
  xor xor_1 (xor_1_out, Count[0], Count[1]);

  assign Q0 = Count[0];
  assign Q1 = Count[1];
endmodule

module PHASE_GENERATOR (
  input  Clock,
  input  Reset,
  output Fetch,
  output Fetch_Write,
  output Execute,
  output Execute_Write
);

  wire [1:0] COUNTER_2BIT_q;

  Counter #(.max('h3), .width(2)) COUNTER_2BIT (
    .clr(Reset), .load(1'b0), .up(1'b1), .count(1'b1), .clk(Clock), .Q(COUNTER_2BIT_q));  // open: D, carry
  Decoder_2to4 decoder_2to4_1 (.AB(COUNTER_2BIT_q), .D0(Fetch), .D1(Fetch_Write), .D2(Execute), .D3(Execute_Write));
endmodule

module safe_write (
  input  [3:0] RD_Addr,
  output SW
);

  wire or_1_out, or_2_out;

  or or_1 (or_1_out, RD_Addr[0], RD_Addr[1]);
  or or_2 (or_2_out, or_1_out, RD_Addr[2]);
  or or_3 (SW, or_2_out, RD_Addr[3]);
endmodule

module Register_File_16x16 (
  input  [3:0] RS_Addr,
  input  [15:0] Write_Data,
  input  Clock,
  input  [3:0] RD_Addr,
  input  REG_WRITE,
  input  [3:0] RT_Addr,
  input  Read_RD_Mux,
  output [15:0] RS_Data,
  output [15:0] RT_Data
);

  wire and_1_out, safe_write_1_sw;
  wire [3:0] hotmux_2to1_4bit_1_o, hotmux_2to1_4bit_2_o, hotmux_2to1_4bit_3_o;

  HOTMUX_2TO1_4BIT hotmux_2to1_4bit_1 (.A(RS_Addr), .B(RD_Addr), .SEL(and_1_out), .O(hotmux_2to1_4bit_1_o));
  safe_write safe_write_1 (.RD_Addr(RD_Addr), .SW(safe_write_1_sw));
  and and_1 (and_1_out, safe_write_1_sw, REG_WRITE);
  RAM #(.addrWidth(4), .asyncread("true"), .dataWidth(16)) RS_RAM (
    .addr(hotmux_2to1_4bit_1_o), .we(and_1_out), .oe(1'b1), .clk(Clock), .din(Write_Data), .dout(RS_Data));
  HOTMUX_2TO1_4BIT hotmux_2to1_4bit_2 (.A(RT_Addr), .B(RD_Addr), .SEL(Read_RD_Mux), .O(hotmux_2to1_4bit_2_o));
  RAM #(.addrWidth(4), .asyncread("true"), .dataWidth(16)) RT_RAM (
    .addr(hotmux_2to1_4bit_3_o), .we(and_1_out), .oe(1'b1), .clk(Clock), .din(Write_Data), .dout(RT_Data));
  HOTMUX_2TO1_4BIT hotmux_2to1_4bit_3 (
    .A(hotmux_2to1_4bit_2_o), .B(RD_Addr), .SEL(and_1_out), .O(hotmux_2to1_4bit_3_o));
endmodule

module Writeback_Buffer_16bit (
  input  [15:0] Data_IN,
  input  Execute,
  output [15:0] Data_out
);

  wire not_1_out;

  not not_1 (not_1_out, Execute);
  Rejister_16bit rejister_16bit_1 (.Data(Data_IN), .Write(1'b1), .Clock(not_1_out), .O(Data_out));
endmodule

module IR_Field_Splitter (
  input  [15:0] IR_IN,
  output [3:0] OPCODE,
  output [3:0] RD,
  output [3:0] RS,
  output [3:0] RT,
  output [7:0] ADDR,
  output [15:0] IMM16
);


  assign ADDR = IR_IN[7:0];
  assign IMM16 = {{8{1'b0}}, IR_IN[7:0]};
  assign OPCODE = IR_IN[15:12];
  assign RD = IR_IN[11:8];
  assign RS = IR_IN[7:4];
  assign RT = IR_IN[3:0];
endmodule

module ALU_B_MUX (
  input  [15:0] RT_DATA,
  input  [15:0] IMM16,
  input  SEL_IMM,
  output [15:0] ALU_B_OUT
);

  hotmux_2to1_16bit hotmux_2to1_16bit_1 (.A(RT_DATA), .B(IMM16), .SEL(SEL_IMM), .O(ALU_B_OUT));
endmodule

module Meomory_Address_mux (
  input  [7:0] PC_ADDR,
  input  [7:0] IR_ADDR,
  input  [15:0] RT_ADDR_VALUE,
  input  SEL_PC,
  input  SEL_IR,
  input  SEL_RT,
  output [7:0] MEM_ADDR
);

  // Probe on RT_ADDR_VALUE[15:8]
  OneHotMux_3to1_8bit onehotmux_3to1_8bit_1 (
    .IN0(PC_ADDR), .IN1(IR_ADDR), .IN2(RT_ADDR_VALUE[7:0]), .SEL_0(SEL_PC), .SEL_1(SEL_IR), .SEL_2(SEL_RT),
    .O(MEM_ADDR));
endmodule

module Writeback_mux (
  input  [15:0] ALU_IN,
  input  [15:0] MEM_IN,
  input  [15:0] PC_LINK_IN,
  input  SEL_ALU,
  input  SEL_MEM,
  input  SEL_PC,
  output [15:0] WRITEBACK_OUT
);

  OneHotMux_3to1_16bit onehotmux_3to1_16bit_1 (
    .IN0(ALU_IN), .IN1(MEM_IN), .IN2(PC_LINK_IN), .SEL_0(SEL_ALU), .SEL_1(SEL_MEM), .SEL_2(SEL_PC),
    .O(WRITEBACK_OUT));
endmodule

module WRITEBACK_FULL_BUFFER (
  input  [15:0] ALU_IN,
  input  [15:0] MEM_IN,
  input  [15:0] PC_LINK_IN,
  input  SEL_ALU,
  input  SEL_MEM,
  input  SEL_PC,
  input  Execute,
  output [15:0] Data_out
);

  wire not_1_out;
  wire [15:0] onehotmux_3to1_16bit_1_o;

  OneHotMux_3to1_16bit onehotmux_3to1_16bit_1 (
    .IN0(ALU_IN), .IN1(MEM_IN), .IN2(PC_LINK_IN), .SEL_0(SEL_ALU), .SEL_1(SEL_MEM), .SEL_2(SEL_PC),
    .O(onehotmux_3to1_16bit_1_o));
  not not_1 (not_1_out, Execute);
  Rejister_16bit rejister_16bit_1 (.Data(onehotmux_3to1_16bit_1_o), .Write(1'b1), .Clock(not_1_out), .O(Data_out));
endmodule

module PC_LOAD_MUX (
  input  [7:0] IR_ADDR,
  input  [15:0] RD_VALUE,
  input  SEL_REG,
  output [7:0] PC_LOAD_OUT
);

  // Probe on RD_VALUE[15:8]
  HOTMUX_2TO1_8BIT hotmux_2to1_8bit_1 (.A(IR_ADDR), .B(RD_VALUE[7:0]), .SEL(SEL_REG), .O(PC_LOAD_OUT));
endmodule

module SHL_16BIT_by1 (
  input  [15:0] In_put,
  output [15:0] O
);


  assign O = {In_put[14:0], 1'b0};
endmodule

module SHL_16BIT_BY2 (
  input  [15:0] In_put,
  output [15:0] O
);


  assign O = {In_put[13:0], 2'b00};
endmodule

module SHL_16BIT_BY4 (
  input  [15:0] In_put,
  output [15:0] O
);


  assign O = {In_put[11:0], 4'b0000};
endmodule

module SHL_16BIT_BY8 (
  input  [15:0] In_put,
  output [15:0] O
);


  assign O = {In_put[7:0], {8{1'b0}}};
endmodule

module SHR_16BIT_BY1 (
  input  [15:0] In_put,
  output [15:0] O
);


  assign O = {1'b0, In_put[15:1]};
endmodule

module SHR_16BIT_BY2 (
  input  [15:0] In_put,
  output [15:0] O
);


  assign O = {2'b00, In_put[15:2]};
endmodule

module SHR_16BIT_BY4 (
  input  [15:0] In_put,
  output [15:0] O
);


  assign O = {4'b0000, In_put[15:4]};
endmodule

module SHR_16BIT_BY8 (
  input  [15:0] In_put,
  output [15:0] O
);


  assign O = {{8{1'b0}}, In_put[15:8]};
endmodule

module SHL_16BIT_VAR (
  input  [15:0] A,
  input  [15:0] B,
  output [15:0] O
);

  wire [15:0] hotmux_2to1_16bit_1_o, hotmux_2to1_16bit_2_o, hotmux_2to1_16bit_3_o, shl_16bit_by1_1_o,
       shl_16bit_by2_1_o, shl_16bit_by4_1_o, shl_16bit_by8_1_o;

  SHL_16BIT_by1 shl_16bit_by1_1 (.In_put(A), .O(shl_16bit_by1_1_o));
  hotmux_2to1_16bit hotmux_2to1_16bit_1 (.A(A), .B(shl_16bit_by1_1_o), .SEL(B[0]), .O(hotmux_2to1_16bit_1_o));
  SHL_16BIT_BY2 shl_16bit_by2_1 (.In_put(hotmux_2to1_16bit_1_o), .O(shl_16bit_by2_1_o));
  SHL_16BIT_BY4 shl_16bit_by4_1 (.In_put(hotmux_2to1_16bit_3_o), .O(shl_16bit_by4_1_o));
  SHL_16BIT_BY8 shl_16bit_by8_1 (.In_put(hotmux_2to1_16bit_2_o), .O(shl_16bit_by8_1_o));
  // Probe on hotmux_2to1_16bit_1_o
  hotmux_2to1_16bit hotmux_2to1_16bit_2 (
    .A(hotmux_2to1_16bit_3_o), .B(shl_16bit_by4_1_o), .SEL(B[2]), .O(hotmux_2to1_16bit_2_o));
  // Probe on hotmux_2to1_16bit_3_o
  hotmux_2to1_16bit hotmux_2to1_16bit_3 (
    .A(hotmux_2to1_16bit_1_o), .B(shl_16bit_by2_1_o), .SEL(B[1]), .O(hotmux_2to1_16bit_3_o));
  hotmux_2to1_16bit hotmux_2to1_16bit_4 (.A(hotmux_2to1_16bit_2_o), .B(shl_16bit_by8_1_o), .SEL(B[3]), .O(O));
  // Probe on hotmux_2to1_16bit_2_o
endmodule

module SHR_16BIT_VAR (
  input  [15:0] A,
  input  [15:0] B,
  output [15:0] O
);

  wire [15:0] hotmux_2to1_16bit_1_o, hotmux_2to1_16bit_2_o, hotmux_2to1_16bit_3_o, shr_16bit_by1_1_o,
       shr_16bit_by2_1_o, shr_16bit_by4_1_o, shr_16bit_by8_1_o;

  SHR_16BIT_BY1 shr_16bit_by1_1 (.In_put(A), .O(shr_16bit_by1_1_o));
  hotmux_2to1_16bit hotmux_2to1_16bit_1 (.A(A), .B(shr_16bit_by1_1_o), .SEL(B[0]), .O(hotmux_2to1_16bit_1_o));
  SHR_16BIT_BY2 shr_16bit_by2_1 (.In_put(hotmux_2to1_16bit_1_o), .O(shr_16bit_by2_1_o));
  SHR_16BIT_BY4 shr_16bit_by4_1 (.In_put(hotmux_2to1_16bit_3_o), .O(shr_16bit_by4_1_o));
  SHR_16BIT_BY8 shr_16bit_by8_1 (.In_put(hotmux_2to1_16bit_2_o), .O(shr_16bit_by8_1_o));
  // Probe on hotmux_2to1_16bit_1_o
  hotmux_2to1_16bit hotmux_2to1_16bit_2 (
    .A(hotmux_2to1_16bit_3_o), .B(shr_16bit_by4_1_o), .SEL(B[2]), .O(hotmux_2to1_16bit_2_o));
  // Probe on hotmux_2to1_16bit_3_o
  hotmux_2to1_16bit hotmux_2to1_16bit_3 (
    .A(hotmux_2to1_16bit_1_o), .B(shr_16bit_by2_1_o), .SEL(B[1]), .O(hotmux_2to1_16bit_3_o));
  hotmux_2to1_16bit hotmux_2to1_16bit_4 (.A(hotmux_2to1_16bit_2_o), .B(shr_16bit_by8_1_o), .SEL(B[3]), .O(O));
  // Probe on hotmux_2to1_16bit_2_o
endmodule

module Control_Unit_TOY16 (
  input  [3:0] OPCODE,
  input  FETCH,
  input  FETCH_WRITE,
  input  EXECUTE,
  input  EXECUTE_WRITE,
  input  ZERO,
  input  POSITIVE,
  output HALT,
  output ALU_ADD,
  output ALU_SUB,
  output ALU_AND,
  output ALU_XOR,
  output ALU_SHL,
  output ALU_SHR,
  output ALU_B_SEL_IMM,
  output ALU_PASS_B,
  output MEM_SEL_IR,
  output MEM_SEL_RT,
  output MEM_WRITE,
  output REG_WRITE,
  output PC_LOAD,
  output PC_WRITE,
  output WB_SEL_ALU,
  output WB_SEL_MEM,
  output WB_SEL_PC,
  output PC_LOAD_REG,
  output IR_WRITE,
  output MEM_SEL_PC,
  output READ_RD_MUX,
  output STORE_INDIRECT
);

  wire and_1_out, and_2_out, and_7_out, and_8_out, D0, D1, D2, D3, D4, D5, D6, D7, D8, D9, D10, D12, D13,
       D14, D15, or_1_out, or_2_out, or_3_out, or_5_out, or_6_out, or_7_out, or_8_out, or_9_out, or_10_out,
       or_11_out, or_12_out, or_13_out, or_14_out;

  Decoder_4to16 decoder_4to16_1 (
    .A0(OPCODE[0]), .A1(OPCODE[1]), .A2(OPCODE[2]), .A3(OPCODE[3]), .D0(D0), .D1(D1), .D2(D2), .D3(D3),
    .D4(D4), .D5(D5), .D6(D6), .D7(D7), .D8(D8), .D9(D9), .D10(D10), .D11(STORE_INDIRECT), .D12(D12),
    .D13(D13), .D14(D14), .D15(D15));
  and and_1 (and_1_out, D12, ZERO);
  and and_2 (and_2_out, D13, POSITIVE);
  or or_1 (or_1_out, and_1_out, D14, and_2_out, D15);
  and and_3 (PC_LOAD, EXECUTE_WRITE, or_1_out);
  or or_2 (or_2_out, D1, D2, D3, D4, D5, D6, D7);
  or or_3 (or_3_out, D8, D10);
  and and_4 (WB_SEL_PC, EXECUTE, D15);
  or or_4 (MEM_SEL_PC, FETCH, FETCH_WRITE);
  or or_5 (or_5_out, D12, D13);
  or or_6 (or_6_out, EXECUTE_WRITE, EXECUTE);
  or or_7 (or_7_out, EXECUTE_WRITE, EXECUTE);
  or or_8 (or_8_out, D8, D9);
  or or_9 (or_9_out, D10, STORE_INDIRECT);
  or or_10 (or_10_out, EXECUTE_WRITE, EXECUTE);
  or or_11 (or_11_out, D9, STORE_INDIRECT);
  or or_12 (or_12_out, D5, D1, D2, D3, D4, D6, D7, D8, D10, D15);
  and and_5 (WB_SEL_ALU, or_2_out, EXECUTE);
  and and_6 (PC_LOAD_REG, EXECUTE_WRITE, D14);
  or or_13 (or_13_out, EXECUTE_WRITE, EXECUTE);
  or or_14 (or_14_out, D9, D12, D13, D14);
  and and_7 (and_7_out, D7, EXECUTE);
  and and_8 (and_8_out, or_5_out, or_6_out);
  and and_9 (MEM_SEL_IR, or_7_out, or_8_out);
  and and_10 (MEM_SEL_RT, or_9_out, or_10_out);
  and and_11 (MEM_WRITE, or_11_out, EXECUTE_WRITE);
  and and_12 (REG_WRITE, or_12_out, EXECUTE_WRITE);
  or or_15 (PC_WRITE, PC_LOAD, FETCH_WRITE);
  and and_13 (WB_SEL_MEM, or_3_out, EXECUTE);
  and and_14 (READ_RD_MUX, or_13_out, or_14_out);
  and and_15 (HALT, D0, EXECUTE);
  and and_16 (ALU_ADD, D1, EXECUTE);
  and and_17 (ALU_SUB, D2, EXECUTE);
  and and_18 (ALU_AND, D3, EXECUTE);
  and and_19 (ALU_XOR, D4, EXECUTE);
  and and_20 (ALU_SHL, D5, EXECUTE);
  and and_21 (ALU_SHR, D6, EXECUTE);
  and and_22 (ALU_B_SEL_IMM, D7, EXECUTE);
  or or_16 (ALU_PASS_B, and_7_out, and_8_out);

  assign IR_WRITE = FETCH_WRITE;

  // Other names for the same wires on the sheet: D11 = STORE_INDIRECT
endmodule

module TOY_16CPU (
  input  RESET,
  output HALT
);

  wire alu_16bit_1_positive, alu_16bit_1_zero, control_unit_toy16_1_alu_add, control_unit_toy16_1_alu_and,
       control_unit_toy16_1_alu_b_sel_imm, control_unit_toy16_1_alu_pass_b, control_unit_toy16_1_alu_shl,
       control_unit_toy16_1_alu_shr, control_unit_toy16_1_alu_sub, control_unit_toy16_1_alu_xor,
       control_unit_toy16_1_ir_write, control_unit_toy16_1_mem_sel_ir, control_unit_toy16_1_mem_sel_pc,
       control_unit_toy16_1_mem_sel_rt, control_unit_toy16_1_mem_write, control_unit_toy16_1_pc_load,
       control_unit_toy16_1_pc_load_reg, control_unit_toy16_1_pc_write, control_unit_toy16_1_read_rd_mux,
       control_unit_toy16_1_reg_write, control_unit_toy16_1_store_indirect, control_unit_toy16_1_wb_sel_alu,
       control_unit_toy16_1_wb_sel_mem, control_unit_toy16_1_wb_sel_pc, Global_Clock_out,
       phase_generator_1_execute, phase_generator_1_execute_write, phase_generator_1_fetch,
       phase_generator_1_fetch_write;
  wire [3:0] hotmux_2to1_4bit_1_o, ir_field_splitter_1_opcode, ir_field_splitter_1_rd,
       ir_field_splitter_1_rs, ir_field_splitter_1_rt;
  wire [7:0] ir_field_splitter_1_addr, meomory_address_mux_1_mem_addr, pc_8bit_1_pc_out,
       pc_load_mux_1_pc_load_out;
  wire [15:0] alu_16bit_1_o, alu_b_mux_1_alu_b_out, hotmux_2to1_16bit_1_o, ir_field_splitter_1_imm16,
       ir_register_16bit_1_ir_out, ram_256x16_1_mem_out, register_file_16x16_1_rs_data,
       register_file_16x16_1_rt_data, writeback_full_buffer_1_data_out;

  Clock Global_Clock (.out(Global_Clock_out));
  PHASE_GENERATOR phase_generator_1 (
    .Clock(Global_Clock_out), .Reset(RESET), .Fetch(phase_generator_1_fetch),
    .Fetch_Write(phase_generator_1_fetch_write), .Execute(phase_generator_1_execute),
    .Execute_Write(phase_generator_1_execute_write));
  PC_8BIT pc_8bit_1 (
    .Load_IN(pc_load_mux_1_pc_load_out), .Load(control_unit_toy16_1_pc_load),
    .Write(control_unit_toy16_1_pc_write), .Clock(Global_Clock_out), .PC_OUT(pc_8bit_1_pc_out));  // open: cout
  PC_LOAD_MUX pc_load_mux_1 (
    .IR_ADDR(ir_field_splitter_1_addr), .RD_VALUE(register_file_16x16_1_rt_data),
    .SEL_REG(control_unit_toy16_1_pc_load_reg), .PC_LOAD_OUT(pc_load_mux_1_pc_load_out));
  IR_Field_Splitter ir_field_splitter_1 (
    .IR_IN(ir_register_16bit_1_ir_out), .OPCODE(ir_field_splitter_1_opcode), .RD(ir_field_splitter_1_rd),
    .RS(ir_field_splitter_1_rs), .RT(ir_field_splitter_1_rt), .ADDR(ir_field_splitter_1_addr),
    .IMM16(ir_field_splitter_1_imm16));
  // Probe on ir_field_splitter_1_rd
  Control_Unit_TOY16 control_unit_toy16_1 (
    .OPCODE(ir_field_splitter_1_opcode), .FETCH(phase_generator_1_fetch),
    .FETCH_WRITE(phase_generator_1_fetch_write), .EXECUTE(phase_generator_1_execute),
    .EXECUTE_WRITE(phase_generator_1_execute_write), .ZERO(alu_16bit_1_zero),
    .POSITIVE(alu_16bit_1_positive), .HALT(HALT), .ALU_ADD(control_unit_toy16_1_alu_add),
    .ALU_SUB(control_unit_toy16_1_alu_sub), .ALU_AND(control_unit_toy16_1_alu_and),
    .ALU_XOR(control_unit_toy16_1_alu_xor), .ALU_SHL(control_unit_toy16_1_alu_shl),
    .ALU_SHR(control_unit_toy16_1_alu_shr), .ALU_B_SEL_IMM(control_unit_toy16_1_alu_b_sel_imm),
    .ALU_PASS_B(control_unit_toy16_1_alu_pass_b), .MEM_SEL_IR(control_unit_toy16_1_mem_sel_ir),
    .MEM_SEL_RT(control_unit_toy16_1_mem_sel_rt), .MEM_WRITE(control_unit_toy16_1_mem_write),
    .REG_WRITE(control_unit_toy16_1_reg_write), .PC_LOAD(control_unit_toy16_1_pc_load),
    .PC_WRITE(control_unit_toy16_1_pc_write), .WB_SEL_ALU(control_unit_toy16_1_wb_sel_alu),
    .WB_SEL_MEM(control_unit_toy16_1_wb_sel_mem), .WB_SEL_PC(control_unit_toy16_1_wb_sel_pc),
    .PC_LOAD_REG(control_unit_toy16_1_pc_load_reg), .IR_WRITE(control_unit_toy16_1_ir_write),
    .MEM_SEL_PC(control_unit_toy16_1_mem_sel_pc), .READ_RD_MUX(control_unit_toy16_1_read_rd_mux),
    .STORE_INDIRECT(control_unit_toy16_1_store_indirect));
  // Probe on control_unit_toy16_1_mem_write
  Meomory_Address_mux meomory_address_mux_1 (
    .PC_ADDR(pc_8bit_1_pc_out), .IR_ADDR(ir_field_splitter_1_addr),
    .RT_ADDR_VALUE(register_file_16x16_1_rt_data), .SEL_PC(control_unit_toy16_1_mem_sel_pc),
    .SEL_IR(control_unit_toy16_1_mem_sel_ir), .SEL_RT(control_unit_toy16_1_mem_sel_rt),
    .MEM_ADDR(meomory_address_mux_1_mem_addr));
  // Probe on control_unit_toy16_1_reg_write
  // Probe on meomory_address_mux_1_mem_addr
  // Probe on hotmux_2to1_16bit_1_o
  RAM_256x16 ram_256x16_1 (
    .Address(meomory_address_mux_1_mem_addr), .MEM_Write(control_unit_toy16_1_mem_write),
    .DATA_IN(hotmux_2to1_16bit_1_o), .Clock(Global_Clock_out), .Mem_Out(ram_256x16_1_mem_out));
  // Probe on ram_256x16_1_mem_out
  // Probe on ir_register_16bit_1_ir_out
  IR_Register_16bit ir_register_16bit_1 (
    .Instruction_In(ram_256x16_1_mem_out), .IR_Write(control_unit_toy16_1_ir_write),
    .Clock(Global_Clock_out), .IR_OUT(ir_register_16bit_1_ir_out));
  WRITEBACK_FULL_BUFFER writeback_full_buffer_1 (
    .ALU_IN(alu_16bit_1_o), .MEM_IN(ram_256x16_1_mem_out), .PC_LINK_IN({{8{1'b0}}, pc_8bit_1_pc_out}),
    .SEL_ALU(control_unit_toy16_1_wb_sel_alu), .SEL_MEM(control_unit_toy16_1_wb_sel_mem),
    .SEL_PC(control_unit_toy16_1_wb_sel_pc), .Execute(phase_generator_1_execute),
    .Data_out(writeback_full_buffer_1_data_out));
  HOTMUX_2TO1_4BIT hotmux_2to1_4bit_1 (
    .A(ir_field_splitter_1_rs), .B(ir_field_splitter_1_rd), .SEL(control_unit_toy16_1_store_indirect),
    .O(hotmux_2to1_4bit_1_o));
  // Probe on writeback_full_buffer_1_data_out
  // Probe on register_file_16x16_1_rs_data
  Register_File_16x16 register_file_16x16_1 (
    .RS_Addr(hotmux_2to1_4bit_1_o), .Write_Data(writeback_full_buffer_1_data_out), .Clock(Global_Clock_out),
    .RD_Addr(ir_field_splitter_1_rd), .REG_WRITE(control_unit_toy16_1_reg_write),
    .RT_Addr(ir_field_splitter_1_rt), .Read_RD_Mux(control_unit_toy16_1_read_rd_mux),
    .RS_Data(register_file_16x16_1_rs_data), .RT_Data(register_file_16x16_1_rt_data));
  // Probe on alu_16bit_1_o
  // Probe on register_file_16x16_1_rt_data
  ALU_16BIT alu_16bit_1 (
    .A(register_file_16x16_1_rs_data), .B(alu_b_mux_1_alu_b_out), .SEL_ADD(control_unit_toy16_1_alu_add),
    .SEL_SUB(control_unit_toy16_1_alu_sub), .SEL_AND(control_unit_toy16_1_alu_and),
    .SEL_XOR(control_unit_toy16_1_alu_xor), .SEL_SHL(control_unit_toy16_1_alu_shl),
    .SEL_SHR(control_unit_toy16_1_alu_shr), .SEL_PASS_B(control_unit_toy16_1_alu_pass_b), .O(alu_16bit_1_o),
    .ZERO(alu_16bit_1_zero), .POSITIVE(alu_16bit_1_positive));  // open: COUT
  ALU_B_MUX alu_b_mux_1 (
    .RT_DATA(register_file_16x16_1_rt_data), .IMM16(ir_field_splitter_1_imm16),
    .SEL_IMM(control_unit_toy16_1_alu_b_sel_imm), .ALU_B_OUT(alu_b_mux_1_alu_b_out));
  hotmux_2to1_16bit hotmux_2to1_16bit_1 (
    .A(register_file_16x16_1_rt_data), .B(register_file_16x16_1_rs_data),
    .SEL(control_unit_toy16_1_store_indirect), .O(hotmux_2to1_16bit_1_o));
endmodule

module Front_Panel_TOY16 (
  input  LOOK,
  input  LOAD,
  input  RUN,
  input  RESET,
  input  Global_Clock,
  input  STEP,
  input  [7:0] PANNEL_ADDR,
  input  [15:0] PANNEL_DATA,
  output FETCH,
  output FETCH_WRITE,
  output EXECUTE,
  output EXECUTE_WRITE,
  output READY,
  output HALT,
  output [15:0] RS_DATA_OUT,
  output [15:0] RT_DATA_OUT,
  output [7:0] RAM_ADDR_OUT,
  output [15:0] ALU_OUT,
  output [15:0] RAM_MEM_OUT,
  output [7:0] PC_OUT,
  output [15:0] IR_OUT
);

  wire alu_16bit_1_positive, alu_16bit_1_zero, and_1_out, and_2_out, and_3_out, control_unit_toy16_1_alu_add,
       control_unit_toy16_1_alu_and, control_unit_toy16_1_alu_b_sel_imm, control_unit_toy16_1_alu_pass_b,
       control_unit_toy16_1_alu_shl, control_unit_toy16_1_alu_shr, control_unit_toy16_1_alu_sub,
       control_unit_toy16_1_alu_xor, control_unit_toy16_1_ir_write, control_unit_toy16_1_mem_sel_ir,
       control_unit_toy16_1_mem_sel_pc, control_unit_toy16_1_mem_sel_rt, control_unit_toy16_1_mem_write,
       control_unit_toy16_1_pc_load, control_unit_toy16_1_pc_load_reg, control_unit_toy16_1_pc_write,
       control_unit_toy16_1_read_rd_mux, control_unit_toy16_1_reg_write, control_unit_toy16_1_store_indirect,
       control_unit_toy16_1_wb_sel_alu, control_unit_toy16_1_wb_sel_mem, control_unit_toy16_1_wb_sel_pc,
       not_2_out, not_3_out, or_1_out, or_2_out, or_3_out;
  wire [3:0] hotmux_2to1_4bit_1_o, ir_field_splitter_1_opcode, ir_field_splitter_1_rd,
       ir_field_splitter_1_rs, ir_field_splitter_1_rt;
  wire [7:0] ir_field_splitter_1_addr, meomory_address_mux_1_mem_addr, pc_load_mux_1_pc_load_out;
  wire [15:0] alu_b_mux_1_alu_b_out, hotmux_2to1_16bit_1_o, hotmux_2to1_16bit_2_o, ir_field_splitter_1_imm16,
       writeback_full_buffer_1_data_out;

  not not_1 (READY, HALT);
  or or_1 (or_1_out, LOOK, LOAD);
  and and_1 (and_1_out, RUN, Global_Clock);
  or or_2 (or_2_out, and_1_out, STEP);
  not not_2 (not_2_out, or_1_out);
  and and_2 (and_2_out, READY, not_2_out, or_2_out);
  PHASE_GENERATOR phase_generator_1 (
    .Clock(and_2_out), .Reset(RESET), .Fetch(FETCH), .Fetch_Write(FETCH_WRITE), .Execute(EXECUTE),
    .Execute_Write(EXECUTE_WRITE));
  PC_8BIT pc_8bit_1 (
    .Load_IN(pc_load_mux_1_pc_load_out), .Load(control_unit_toy16_1_pc_load),
    .Write(control_unit_toy16_1_pc_write), .Clock(and_2_out), .PC_OUT(PC_OUT));  // open: cout
  PC_LOAD_MUX pc_load_mux_1 (
    .IR_ADDR(ir_field_splitter_1_addr), .RD_VALUE(RT_DATA_OUT), .SEL_REG(control_unit_toy16_1_pc_load_reg),
    .PC_LOAD_OUT(pc_load_mux_1_pc_load_out));
  IR_Field_Splitter ir_field_splitter_1 (
    .IR_IN(IR_OUT), .OPCODE(ir_field_splitter_1_opcode), .RD(ir_field_splitter_1_rd),
    .RS(ir_field_splitter_1_rs), .RT(ir_field_splitter_1_rt), .ADDR(ir_field_splitter_1_addr),
    .IMM16(ir_field_splitter_1_imm16));
  // Probe on PC_OUT
  // Probe on ir_field_splitter_1_rd
  // Probe on PANNEL_DATA
  Control_Unit_TOY16 control_unit_toy16_1 (
    .OPCODE(ir_field_splitter_1_opcode), .FETCH(FETCH), .FETCH_WRITE(FETCH_WRITE), .EXECUTE(EXECUTE),
    .EXECUTE_WRITE(EXECUTE_WRITE), .ZERO(alu_16bit_1_zero), .POSITIVE(alu_16bit_1_positive), .HALT(HALT),
    .ALU_ADD(control_unit_toy16_1_alu_add), .ALU_SUB(control_unit_toy16_1_alu_sub),
    .ALU_AND(control_unit_toy16_1_alu_and), .ALU_XOR(control_unit_toy16_1_alu_xor),
    .ALU_SHL(control_unit_toy16_1_alu_shl), .ALU_SHR(control_unit_toy16_1_alu_shr),
    .ALU_B_SEL_IMM(control_unit_toy16_1_alu_b_sel_imm), .ALU_PASS_B(control_unit_toy16_1_alu_pass_b),
    .MEM_SEL_IR(control_unit_toy16_1_mem_sel_ir), .MEM_SEL_RT(control_unit_toy16_1_mem_sel_rt),
    .MEM_WRITE(control_unit_toy16_1_mem_write), .REG_WRITE(control_unit_toy16_1_reg_write),
    .PC_LOAD(control_unit_toy16_1_pc_load), .PC_WRITE(control_unit_toy16_1_pc_write),
    .WB_SEL_ALU(control_unit_toy16_1_wb_sel_alu), .WB_SEL_MEM(control_unit_toy16_1_wb_sel_mem),
    .WB_SEL_PC(control_unit_toy16_1_wb_sel_pc), .PC_LOAD_REG(control_unit_toy16_1_pc_load_reg),
    .IR_WRITE(control_unit_toy16_1_ir_write), .MEM_SEL_PC(control_unit_toy16_1_mem_sel_pc),
    .READ_RD_MUX(control_unit_toy16_1_read_rd_mux), .STORE_INDIRECT(control_unit_toy16_1_store_indirect));
  Meomory_Address_mux meomory_address_mux_1 (
    .PC_ADDR(PC_OUT), .IR_ADDR(ir_field_splitter_1_addr), .RT_ADDR_VALUE(RT_DATA_OUT),
    .SEL_PC(control_unit_toy16_1_mem_sel_pc), .SEL_IR(control_unit_toy16_1_mem_sel_ir),
    .SEL_RT(control_unit_toy16_1_mem_sel_rt), .MEM_ADDR(meomory_address_mux_1_mem_addr));
  // Probe on control_unit_toy16_1_reg_write
  // Probe on hotmux_2to1_16bit_1_o
  // Probe on PANNEL_ADDR
  // Probe on nothing
  hotmux_2to1_16bit hotmux_2to1_16bit_1 (
    .A(hotmux_2to1_16bit_2_o), .B(PANNEL_DATA), .SEL(LOAD), .O(hotmux_2to1_16bit_1_o));
  not not_3 (not_3_out, or_1_out);
  and and_3 (and_3_out, control_unit_toy16_1_mem_write, not_3_out);
  // Probe on RAM_ADDR_OUT
  or or_3 (or_3_out, and_3_out, LOAD);
  // Probe on or_3_out
  RAM_256x16 ram_256x16_1 (
    .Address(RAM_ADDR_OUT), .MEM_Write(or_3_out), .DATA_IN(hotmux_2to1_16bit_1_o), .Clock(or_2_out),
    .Mem_Out(RAM_MEM_OUT));
  // Probe on RAM_MEM_OUT
  HOTMUX_2TO1_8BIT hotmux_2to1_8bit_1 (
    .A(meomory_address_mux_1_mem_addr), .B(PANNEL_ADDR), .SEL(or_1_out), .O(RAM_ADDR_OUT));
  // Probe on IR_OUT
  IR_Register_16bit ir_register_16bit_1 (
    .Instruction_In(RAM_MEM_OUT), .IR_Write(control_unit_toy16_1_ir_write), .Clock(and_2_out), .IR_OUT(IR_OUT));
  WRITEBACK_FULL_BUFFER writeback_full_buffer_1 (
    .ALU_IN(ALU_OUT), .MEM_IN(RAM_MEM_OUT), .PC_LINK_IN({{8{1'b0}}, PC_OUT}),
    .SEL_ALU(control_unit_toy16_1_wb_sel_alu), .SEL_MEM(control_unit_toy16_1_wb_sel_mem),
    .SEL_PC(control_unit_toy16_1_wb_sel_pc), .Execute(EXECUTE), .Data_out(writeback_full_buffer_1_data_out));
  HOTMUX_2TO1_4BIT hotmux_2to1_4bit_1 (
    .A(ir_field_splitter_1_rs), .B(ir_field_splitter_1_rd), .SEL(control_unit_toy16_1_store_indirect),
    .O(hotmux_2to1_4bit_1_o));
  // Probe on writeback_full_buffer_1_data_out
  // Probe on RS_DATA_OUT
  // Probe on RT_DATA_OUT
  Register_File_16x16 register_file_16x16_1 (
    .RS_Addr(hotmux_2to1_4bit_1_o), .Write_Data(writeback_full_buffer_1_data_out), .Clock(and_2_out),
    .RD_Addr(ir_field_splitter_1_rd), .REG_WRITE(control_unit_toy16_1_reg_write),
    .RT_Addr(ir_field_splitter_1_rt), .Read_RD_Mux(control_unit_toy16_1_read_rd_mux), .RS_Data(RS_DATA_OUT),
    .RT_Data(RT_DATA_OUT));
  // Probe on ALU_OUT
  ALU_16BIT alu_16bit_1 (
    .A(RS_DATA_OUT), .B(alu_b_mux_1_alu_b_out), .SEL_ADD(control_unit_toy16_1_alu_add),
    .SEL_SUB(control_unit_toy16_1_alu_sub), .SEL_AND(control_unit_toy16_1_alu_and),
    .SEL_XOR(control_unit_toy16_1_alu_xor), .SEL_SHL(control_unit_toy16_1_alu_shl),
    .SEL_SHR(control_unit_toy16_1_alu_shr), .SEL_PASS_B(control_unit_toy16_1_alu_pass_b), .O(ALU_OUT),
    .ZERO(alu_16bit_1_zero), .POSITIVE(alu_16bit_1_positive));  // open: COUT
  ALU_B_MUX alu_b_mux_1 (
    .RT_DATA(RT_DATA_OUT), .IMM16(ir_field_splitter_1_imm16), .SEL_IMM(control_unit_toy16_1_alu_b_sel_imm),
    .ALU_B_OUT(alu_b_mux_1_alu_b_out));
  hotmux_2to1_16bit hotmux_2to1_16bit_2 (
    .A(RT_DATA_OUT), .B(RS_DATA_OUT), .SEL(control_unit_toy16_1_store_indirect), .O(hotmux_2to1_16bit_2_o));
endmodule
module Main_Pannel_TOY_16 (
  input  LOOK,
  input  RUN,
  input  STEP,
  input  LOAD,
  input  RESET,
  input  [7:0] PANNEL_ADDR,
  input  [15:0] PANNEL_DATA
);

  wire clock_1_out, front_panel_toy16_1_execute, front_panel_toy16_1_execute_write,
       front_panel_toy16_1_fetch, front_panel_toy16_1_fetch_write, front_panel_toy16_1_halt,
       front_panel_toy16_1_ready;
  wire [7:0] front_panel_toy16_1_pc_out, front_panel_toy16_1_ram_addr_out;
  wire [15:0] front_panel_toy16_1_alu_out, front_panel_toy16_1_ir_out, front_panel_toy16_1_ram_mem_out,
       front_panel_toy16_1_rs_data_out, front_panel_toy16_1_rt_data_out;

  Clock clock_1 (.out(clock_1_out));
  LED led_1 (.in(LOOK));
  LED led_2 (.in(LOAD));
  LED led_3 (.in(RUN));
  LED led_4 (.in(RESET));
  LED led_5 (.in(PANNEL_ADDR[7]));
  LED led_6 (.in(PANNEL_DATA[15]));
  LED led_7 (.in(PANNEL_DATA[14]));
  Hex_Digit_Display hex_digit_display_1 (.value(PANNEL_DATA[15:12]));  // open: dp
  LED led_8 (.in(PANNEL_ADDR[6]));
  LED led_9 (.in(PANNEL_ADDR[5]));
  LED led_10 (.in(PANNEL_ADDR[4]));
  LED led_11 (.in(PANNEL_DATA[13]));
  LED led_12 (.in(PANNEL_DATA[12]));
  Hex_Digit_Display hex_digit_display_2 (.value(PANNEL_DATA[11:8]));  // open: dp
  Hex_Digit_Display hex_digit_display_3 (.value(PANNEL_DATA[7:4]));  // open: dp
  LED led_13 (.in(PANNEL_ADDR[3]));
  LED led_14 (.in(PANNEL_ADDR[2]));
  LED led_15 (.in(PANNEL_ADDR[1]));
  LED led_16 (.in(PANNEL_DATA[11]));
  LED led_17 (.in(PANNEL_DATA[10]));
  LED led_18 (.in(PANNEL_DATA[9]));
  Hex_Digit_Display hex_digit_display_4 (.value(PANNEL_DATA[3:0]));  // open: dp
  LED led_19 (.in(PANNEL_ADDR[0]));
  LED led_20 (.in(PANNEL_DATA[8]));
  LED led_21 (.in(PANNEL_DATA[7]));
  LED led_22 (.in(PANNEL_DATA[6]));
  Hex_Digit_Display hex_digit_display_5 (.value(PANNEL_ADDR[7:4]));  // open: dp
  LED led_23 (.in(PANNEL_DATA[5]));
  LED led_24 (.in(PANNEL_DATA[4]));
  LED led_25 (.in(front_panel_toy16_1_fetch));
  LED led_26 (.in(front_panel_toy16_1_fetch_write));
  Front_Panel_TOY16 front_panel_toy16_1 (
    .LOOK(LOOK), .LOAD(LOAD), .RUN(RUN), .RESET(RESET), .Global_Clock(clock_1_out), .STEP(STEP),
    .PANNEL_ADDR(PANNEL_ADDR), .PANNEL_DATA(PANNEL_DATA), .FETCH(front_panel_toy16_1_fetch),
    .FETCH_WRITE(front_panel_toy16_1_fetch_write), .EXECUTE(front_panel_toy16_1_execute),
    .EXECUTE_WRITE(front_panel_toy16_1_execute_write), .READY(front_panel_toy16_1_ready),
    .HALT(front_panel_toy16_1_halt), .RS_DATA_OUT(front_panel_toy16_1_rs_data_out),
    .RT_DATA_OUT(front_panel_toy16_1_rt_data_out), .RAM_ADDR_OUT(front_panel_toy16_1_ram_addr_out),
    .ALU_OUT(front_panel_toy16_1_alu_out), .RAM_MEM_OUT(front_panel_toy16_1_ram_mem_out),
    .PC_OUT(front_panel_toy16_1_pc_out), .IR_OUT(front_panel_toy16_1_ir_out));
  Hex_Digit_Display hex_digit_display_6 (.value(PANNEL_ADDR[3:0]));  // open: dp
  LED led_27 (.in(PANNEL_DATA[1]));
  LED led_28 (.in(PANNEL_DATA[3]));
  LED led_29 (.in(PANNEL_DATA[2]));
  LED led_30 (.in(front_panel_toy16_1_execute));
  LED led_31 (.in(front_panel_toy16_1_execute_write));
  LED led_32 (.in(PANNEL_DATA[0]));
  LED led_33 (.in(front_panel_toy16_1_halt));
  LED led_34 (.in(front_panel_toy16_1_ready));
  Hex_Digit_Display hex_digit_display_7 (.value(front_panel_toy16_1_rs_data_out[15:12]));  // open: dp
  Hex_Digit_Display hex_digit_display_8 (.value(front_panel_toy16_1_rs_data_out[11:8]));  // open: dp
  Hex_Digit_Display hex_digit_display_9 (.value(front_panel_toy16_1_rt_data_out[15:12]));  // open: dp
  Hex_Digit_Display hex_digit_display_10 (.value(front_panel_toy16_1_rt_data_out[11:8]));  // open: dp
  Hex_Digit_Display hex_digit_display_11 (.value(front_panel_toy16_1_ram_addr_out[7:4]));  // open: dp
  Hex_Digit_Display hex_digit_display_12 (.value(front_panel_toy16_1_ram_addr_out[3:0]));  // open: dp
  Hex_Digit_Display hex_digit_display_13 (.value(front_panel_toy16_1_alu_out[15:12]));  // open: dp
  Hex_Digit_Display hex_digit_display_14 (.value(front_panel_toy16_1_alu_out[11:8]));  // open: dp
  Hex_Digit_Display hex_digit_display_15 (.value(front_panel_toy16_1_ram_mem_out[15:12]));  // open: dp
  Hex_Digit_Display hex_digit_display_16 (.value(front_panel_toy16_1_ram_mem_out[11:8]));  // open: dp
  Hex_Digit_Display hex_digit_display_17 (.value(front_panel_toy16_1_pc_out[7:4]));  // open: dp
  Hex_Digit_Display hex_digit_display_18 (.value(front_panel_toy16_1_pc_out[3:0]));  // open: dp
  Hex_Digit_Display hex_digit_display_19 (.value(front_panel_toy16_1_ir_out[15:12]));  // open: dp
  Hex_Digit_Display hex_digit_display_20 (.value(front_panel_toy16_1_ir_out[11:8]));  // open: dp
  Hex_Digit_Display hex_digit_display_21 (.value(front_panel_toy16_1_rs_data_out[7:4]));  // open: dp
  Hex_Digit_Display hex_digit_display_22 (.value(front_panel_toy16_1_rt_data_out[7:4]));  // open: dp
  Hex_Digit_Display hex_digit_display_23 (.value(front_panel_toy16_1_alu_out[7:4]));  // open: dp
  Hex_Digit_Display hex_digit_display_24 (.value(front_panel_toy16_1_ram_mem_out[7:4]));  // open: dp
  Hex_Digit_Display hex_digit_display_25 (.value(front_panel_toy16_1_ir_out[7:4]));  // open: dp
  Hex_Digit_Display hex_digit_display_26 (.value(front_panel_toy16_1_ir_out[3:0]));  // open: dp
  Hex_Digit_Display hex_digit_display_27 (.value(front_panel_toy16_1_rs_data_out[3:0]));  // open: dp
  Hex_Digit_Display hex_digit_display_28 (.value(front_panel_toy16_1_rt_data_out[3:0]));  // open: dp
  Hex_Digit_Display hex_digit_display_29 (.value(front_panel_toy16_1_alu_out[3:0]));  // open: dp
  Hex_Digit_Display hex_digit_display_30 (.value(front_panel_toy16_1_ram_mem_out[3:0]));  // open: dp
  // Probe on front_panel_toy16_1_rs_data_out
  // Probe on front_panel_toy16_1_rt_data_out
  // Probe on front_panel_toy16_1_ram_addr_out
  // Probe on front_panel_toy16_1_alu_out
  // Probe on front_panel_toy16_1_ram_mem_out
  // Probe on front_panel_toy16_1_pc_out
  // Probe on front_panel_toy16_1_ir_out
endmodule
